// Logisim project SAP_01.circ as structural Verilog: 22 circuits, main circuit program_cointer
module program_cointer (
  input  Ep,
  input  Cp,
  input  CLK,
  input  CLR,
  output [3:0] out_5
);

  wire not_1_out, t_ff_1_qn, t_ff_2_qn, t_ff_3_qn;
  wire [3:0] t_ff_1_q;

  T_Flip_Flop t_ff_1 (.T(Cp), .clk(not_1_out), .Q(t_ff_1_q[0]), .Qn(t_ff_1_qn), .reset(CLR));  // open: preset
  not not_1 (not_1_out, CLK);
  T_Flip_Flop t_ff_2 (.T(Cp), .clk(t_ff_1_qn), .Q(t_ff_1_q[1]), .Qn(t_ff_2_qn), .reset(CLR));  // open: preset
  T_Flip_Flop t_ff_3 (.T(Cp), .clk(t_ff_2_qn), .Q(t_ff_1_q[2]), .Qn(t_ff_3_qn), .reset(CLR));  // open: preset
  T_Flip_Flop t_ff_4 (.T(Cp), .clk(t_ff_3_qn), .Q(t_ff_1_q[3]), .reset(CLR));  // open: Qn, preset
  assign out_5 = Ep ? t_ff_1_q : 4'bz;  // Controlled_Buffer controlled_buffer_1
endmodule

module MAR (
  input  [3:0] in_1,
  input  Lm,
  input  CLK,
  output [3:0] out_4
);

  wire controlled_buffer_1_out, controlled_buffer_2_out, controlled_buffer_3_out, controlled_buffer_4_out;

  D_Flip_Flop d_ff_1 (.D(controlled_buffer_1_out), .clk(CLK), .Q(out_4[0]));  // open: Qn, preset, reset
  assign controlled_buffer_1_out = Lm ? in_1[0] : 1'bz;  // Controlled_Buffer controlled_buffer_1
  D_Flip_Flop d_ff_2 (.D(controlled_buffer_2_out), .clk(CLK), .Q(out_4[1]));  // open: Qn, preset, reset
  assign controlled_buffer_2_out = Lm ? in_1[1] : 1'bz;  // Controlled_Buffer controlled_buffer_2
  D_Flip_Flop d_ff_3 (.D(controlled_buffer_3_out), .clk(CLK), .Q(out_4[2]));  // open: Qn, preset, reset
  assign controlled_buffer_3_out = Lm ? in_1[2] : 1'bz;  // Controlled_Buffer controlled_buffer_3
  D_Flip_Flop d_ff_4 (.D(controlled_buffer_4_out), .clk(CLK), .Q(out_4[3]));  // open: Qn, preset, reset
  assign controlled_buffer_4_out = Lm ? in_1[3] : 1'bz;  // Controlled_Buffer controlled_buffer_4
endmodule

module Register_8bits (
  input  [7:0] in_1,
  input  Li,
  input  Ei,
  input  CLR,
  input  CLK,
  output [7:0] out_6
);

  wire controlled_buffer_1_out, controlled_buffer_2_out, controlled_buffer_3_out, controlled_buffer_4_out,
       controlled_buffer_5_out, controlled_buffer_6_out, controlled_buffer_7_out, controlled_buffer_8_out,
       d_ff_1_q, d_ff_2_q, d_ff_3_q, d_ff_4_q, d_ff_5_q, d_ff_6_q, d_ff_7_q, d_ff_8_q;

  D_Flip_Flop #(.trigger("high")) d_ff_1 (
    .D(controlled_buffer_1_out), .clk(CLK), .Q(d_ff_1_q), .reset(CLR));  // open: Qn, preset
  assign controlled_buffer_1_out = Li ? in_1[0] : 1'bz;  // Controlled_Buffer controlled_buffer_1
  D_Flip_Flop #(.trigger("high")) d_ff_2 (
    .D(controlled_buffer_2_out), .clk(CLK), .Q(d_ff_2_q), .reset(CLR));  // open: Qn, preset
  assign controlled_buffer_2_out = Li ? in_1[1] : 1'bz;  // Controlled_Buffer controlled_buffer_2
  D_Flip_Flop #(.trigger("high")) d_ff_3 (
    .D(controlled_buffer_3_out), .clk(CLK), .Q(d_ff_3_q), .reset(CLR));  // open: Qn, preset
  assign controlled_buffer_3_out = Li ? in_1[2] : 1'bz;  // Controlled_Buffer controlled_buffer_3
  D_Flip_Flop #(.trigger("high")) d_ff_4 (
    .D(controlled_buffer_4_out), .clk(CLK), .Q(d_ff_4_q), .reset(CLR));  // open: Qn, preset
  assign controlled_buffer_4_out = Li ? in_1[3] : 1'bz;  // Controlled_Buffer controlled_buffer_4
  D_Flip_Flop #(.trigger("high")) d_ff_5 (
    .D(controlled_buffer_5_out), .clk(CLK), .Q(d_ff_5_q), .reset(CLR));  // open: Qn, preset
  assign controlled_buffer_5_out = Li ? in_1[4] : 1'bz;  // Controlled_Buffer controlled_buffer_5
  D_Flip_Flop #(.trigger("high")) d_ff_6 (
    .D(controlled_buffer_6_out), .clk(CLK), .Q(d_ff_6_q), .reset(CLR));  // open: Qn, preset
  assign controlled_buffer_6_out = Li ? in_1[5] : 1'bz;  // Controlled_Buffer controlled_buffer_6
  D_Flip_Flop #(.trigger("high")) d_ff_7 (
    .D(controlled_buffer_7_out), .clk(CLK), .Q(d_ff_7_q), .reset(CLR));  // open: Qn, preset
  assign controlled_buffer_7_out = Li ? in_1[6] : 1'bz;  // Controlled_Buffer controlled_buffer_7
  D_Flip_Flop #(.trigger("high")) d_ff_8 (
    .D(controlled_buffer_8_out), .clk(CLK), .Q(d_ff_8_q), .reset(CLR));  // open: Qn, preset
  assign controlled_buffer_8_out = Li ? in_1[7] : 1'bz;  // Controlled_Buffer controlled_buffer_8
  assign out_6[0] = Ei ? d_ff_1_q : 1'bz;  // Controlled_Buffer controlled_buffer_9
  assign out_6[1] = Ei ? d_ff_2_q : 1'bz;  // Controlled_Buffer controlled_buffer_10
  assign out_6[2] = Ei ? d_ff_3_q : 1'bz;  // Controlled_Buffer controlled_buffer_11
  assign out_6[3] = Ei ? d_ff_4_q : 1'bz;  // Controlled_Buffer controlled_buffer_12
  assign out_6[4] = Ei ? d_ff_5_q : 1'bz;  // Controlled_Buffer controlled_buffer_13
  assign out_6[5] = Ei ? d_ff_6_q : 1'bz;  // Controlled_Buffer controlled_buffer_14
  assign out_6[6] = Ei ? d_ff_7_q : 1'bz;  // Controlled_Buffer controlled_buffer_15
  assign out_6[7] = Ei ? d_ff_8_q : 1'bz;  // Controlled_Buffer controlled_buffer_16
endmodule

module RAM_16x8 (
  input  Ce,
  input  [3:0] IN1,
  output [7:0] OUT1
);

  wire dipswitch_1_sw1, dipswitch_1_sw2, dipswitch_1_sw3, dipswitch_1_sw4, dipswitch_1_sw5, dipswitch_1_sw6,
       dipswitch_1_sw7, dipswitch_1_sw8, dipswitch_2_sw1, dipswitch_2_sw2, dipswitch_2_sw3, dipswitch_2_sw4,
       dipswitch_2_sw5, dipswitch_2_sw6, dipswitch_2_sw7, dipswitch_2_sw8, dipswitch_3_sw1, dipswitch_3_sw2,
       dipswitch_3_sw3, dipswitch_3_sw4, dipswitch_3_sw5, dipswitch_3_sw6, dipswitch_3_sw7, dipswitch_3_sw8,
       dipswitch_4_sw1, dipswitch_4_sw2, dipswitch_4_sw3, dipswitch_4_sw4, dipswitch_4_sw5, dipswitch_4_sw6,
       dipswitch_4_sw7, dipswitch_4_sw8, dipswitch_5_sw1, dipswitch_5_sw2, dipswitch_5_sw3, dipswitch_5_sw4,
       dipswitch_5_sw5, dipswitch_5_sw6, dipswitch_5_sw7, dipswitch_5_sw8, dipswitch_6_sw1, dipswitch_6_sw2,
       dipswitch_6_sw3, dipswitch_6_sw4, dipswitch_6_sw5, dipswitch_6_sw6, dipswitch_6_sw7, dipswitch_6_sw8,
       dipswitch_7_sw1, dipswitch_7_sw2, dipswitch_7_sw3, dipswitch_7_sw4, dipswitch_7_sw5, dipswitch_7_sw6,
       dipswitch_7_sw7, dipswitch_7_sw8, dipswitch_8_sw1, dipswitch_8_sw2, dipswitch_8_sw3, dipswitch_8_sw4,
       dipswitch_8_sw5, dipswitch_8_sw6, dipswitch_8_sw7, dipswitch_8_sw8, dipswitch_9_sw1, dipswitch_9_sw2,
       dipswitch_9_sw3, dipswitch_9_sw4, dipswitch_9_sw5, dipswitch_9_sw6, dipswitch_9_sw7, dipswitch_9_sw8,
       dipswitch_10_sw1, dipswitch_10_sw2, dipswitch_10_sw3, dipswitch_10_sw4, dipswitch_10_sw5,
       dipswitch_10_sw6, dipswitch_10_sw7, dipswitch_10_sw8, dipswitch_11_sw1, dipswitch_11_sw2,
       dipswitch_11_sw3, dipswitch_11_sw4, dipswitch_11_sw5, dipswitch_11_sw6, dipswitch_11_sw7,
       dipswitch_11_sw8, dipswitch_12_sw1, dipswitch_12_sw2, dipswitch_12_sw3, dipswitch_12_sw4,
       dipswitch_12_sw5, dipswitch_12_sw6, dipswitch_12_sw7, dipswitch_12_sw8, dipswitch_13_sw1,
       dipswitch_13_sw2, dipswitch_13_sw3, dipswitch_13_sw4, dipswitch_13_sw5, dipswitch_13_sw6,
       dipswitch_13_sw7, dipswitch_13_sw8, dipswitch_14_sw1, dipswitch_14_sw2, dipswitch_14_sw3,
       dipswitch_14_sw4, dipswitch_14_sw5, dipswitch_14_sw6, dipswitch_14_sw7, dipswitch_14_sw8,
       dipswitch_15_sw1, dipswitch_15_sw2, dipswitch_15_sw3, dipswitch_15_sw4, dipswitch_15_sw5,
       dipswitch_15_sw6, dipswitch_15_sw7, dipswitch_15_sw8, dipswitch_16_sw1, dipswitch_16_sw2,
       dipswitch_16_sw3, dipswitch_16_sw4, dipswitch_16_sw5, dipswitch_16_sw6, dipswitch_16_sw7,
       dipswitch_16_sw8;
  wire [7:0] demultiplexer_1_out0, demultiplexer_1_out8;

  Demultiplexer #(.select(4)) demultiplexer_1 (
    .out0(demultiplexer_1_out0[0]), .out1(demultiplexer_1_out0[1]), .out2(demultiplexer_1_out0[2]),
    .out3(demultiplexer_1_out0[3]), .out4(demultiplexer_1_out0[4]), .out5(demultiplexer_1_out0[5]),
    .out6(demultiplexer_1_out0[6]), .out7(demultiplexer_1_out0[7]), .out8(demultiplexer_1_out8[0]),
    .out9(demultiplexer_1_out8[1]), .out10(demultiplexer_1_out8[2]), .out11(demultiplexer_1_out8[3]),
    .out12(demultiplexer_1_out8[4]), .out13(demultiplexer_1_out8[5]), .out14(demultiplexer_1_out8[6]),
    .out15(demultiplexer_1_out8[7]), .in(Ce), .sel(IN1));
  DipSwitch dipswitch_1 (
    .sw1(dipswitch_1_sw1), .sw2(dipswitch_1_sw2), .sw3(dipswitch_1_sw3), .sw4(dipswitch_1_sw4),
    .sw5(dipswitch_1_sw5), .sw6(dipswitch_1_sw6), .sw7(dipswitch_1_sw7), .sw8(dipswitch_1_sw8));
  DipSwitch dipswitch_2 (
    .sw1(dipswitch_2_sw1), .sw2(dipswitch_2_sw2), .sw3(dipswitch_2_sw3), .sw4(dipswitch_2_sw4),
    .sw5(dipswitch_2_sw5), .sw6(dipswitch_2_sw6), .sw7(dipswitch_2_sw7), .sw8(dipswitch_2_sw8));
  DipSwitch dipswitch_3 (
    .sw1(dipswitch_3_sw1), .sw2(dipswitch_3_sw2), .sw3(dipswitch_3_sw3), .sw4(dipswitch_3_sw4),
    .sw5(dipswitch_3_sw5), .sw6(dipswitch_3_sw6), .sw7(dipswitch_3_sw7), .sw8(dipswitch_3_sw8));
  DipSwitch dipswitch_4 (
    .sw1(dipswitch_4_sw1), .sw2(dipswitch_4_sw2), .sw3(dipswitch_4_sw3), .sw4(dipswitch_4_sw4),
    .sw5(dipswitch_4_sw5), .sw6(dipswitch_4_sw6), .sw7(dipswitch_4_sw7), .sw8(dipswitch_4_sw8));
  DipSwitch dipswitch_5 (
    .sw1(dipswitch_5_sw1), .sw2(dipswitch_5_sw2), .sw3(dipswitch_5_sw3), .sw4(dipswitch_5_sw4),
    .sw5(dipswitch_5_sw5), .sw6(dipswitch_5_sw6), .sw7(dipswitch_5_sw7), .sw8(dipswitch_5_sw8));
  DipSwitch dipswitch_6 (
    .sw1(dipswitch_6_sw1), .sw2(dipswitch_6_sw2), .sw3(dipswitch_6_sw3), .sw4(dipswitch_6_sw4),
    .sw5(dipswitch_6_sw5), .sw6(dipswitch_6_sw6), .sw7(dipswitch_6_sw7), .sw8(dipswitch_6_sw8));
  DipSwitch dipswitch_7 (
    .sw1(dipswitch_7_sw1), .sw2(dipswitch_7_sw2), .sw3(dipswitch_7_sw3), .sw4(dipswitch_7_sw4),
    .sw5(dipswitch_7_sw5), .sw6(dipswitch_7_sw6), .sw7(dipswitch_7_sw7), .sw8(dipswitch_7_sw8));
  DipSwitch dipswitch_8 (
    .sw1(dipswitch_8_sw1), .sw2(dipswitch_8_sw2), .sw3(dipswitch_8_sw3), .sw4(dipswitch_8_sw4),
    .sw5(dipswitch_8_sw5), .sw6(dipswitch_8_sw6), .sw7(dipswitch_8_sw7), .sw8(dipswitch_8_sw8));
  register_RAM h0 (
    .in_1(dipswitch_1_sw8), .in_2(dipswitch_1_sw7), .in_3(dipswitch_1_sw6), .in_4(dipswitch_1_sw5),
    .in_6(dipswitch_1_sw4), .in_7(dipswitch_1_sw3), .in_8(dipswitch_1_sw2), .in_9(dipswitch_1_sw1),
    .in_5(demultiplexer_1_out0[0]), .out_10(OUT1));
  register_RAM h1 (
    .in_1(dipswitch_2_sw8), .in_2(dipswitch_2_sw7), .in_3(dipswitch_2_sw6), .in_4(dipswitch_2_sw5),
    .in_6(dipswitch_2_sw4), .in_7(dipswitch_2_sw3), .in_8(dipswitch_2_sw2), .in_9(dipswitch_2_sw1),
    .in_5(demultiplexer_1_out0[1]), .out_10(OUT1));
  register_RAM h2 (
    .in_1(dipswitch_3_sw8), .in_2(dipswitch_3_sw7), .in_3(dipswitch_3_sw6), .in_4(dipswitch_3_sw5),
    .in_6(dipswitch_3_sw4), .in_7(dipswitch_3_sw3), .in_8(dipswitch_3_sw2), .in_9(dipswitch_3_sw1),
    .in_5(demultiplexer_1_out0[2]), .out_10(OUT1));
  register_RAM h3 (
    .in_1(dipswitch_4_sw8), .in_2(dipswitch_4_sw7), .in_3(dipswitch_4_sw6), .in_4(dipswitch_4_sw5),
    .in_6(dipswitch_4_sw4), .in_7(dipswitch_4_sw3), .in_8(dipswitch_4_sw2), .in_9(dipswitch_4_sw1),
    .in_5(demultiplexer_1_out0[3]), .out_10(OUT1));
  register_RAM h4 (
    .in_1(dipswitch_5_sw8), .in_2(dipswitch_5_sw7), .in_3(dipswitch_5_sw6), .in_4(dipswitch_5_sw5),
    .in_6(dipswitch_5_sw4), .in_7(dipswitch_5_sw3), .in_8(dipswitch_5_sw2), .in_9(dipswitch_5_sw1),
    .in_5(demultiplexer_1_out0[4]), .out_10(OUT1));
  register_RAM h5 (
    .in_1(dipswitch_6_sw8), .in_2(dipswitch_6_sw7), .in_3(dipswitch_6_sw6), .in_4(dipswitch_6_sw5),
    .in_6(dipswitch_6_sw4), .in_7(dipswitch_6_sw3), .in_8(dipswitch_6_sw2), .in_9(dipswitch_6_sw1),
    .in_5(demultiplexer_1_out0[5]), .out_10(OUT1));
  register_RAM h6 (
    .in_1(dipswitch_7_sw8), .in_2(dipswitch_7_sw7), .in_3(dipswitch_7_sw6), .in_4(dipswitch_7_sw5),
    .in_6(dipswitch_7_sw4), .in_7(dipswitch_7_sw3), .in_8(dipswitch_7_sw2), .in_9(dipswitch_7_sw1),
    .in_5(demultiplexer_1_out0[6]), .out_10(OUT1));
  register_RAM h7 (
    .in_1(dipswitch_8_sw8), .in_2(dipswitch_8_sw7), .in_3(dipswitch_8_sw6), .in_4(dipswitch_8_sw5),
    .in_6(dipswitch_8_sw4), .in_7(dipswitch_8_sw3), .in_8(dipswitch_8_sw2), .in_9(dipswitch_8_sw1),
    .in_5(demultiplexer_1_out0[7]), .out_10(OUT1));
  DipSwitch dipswitch_9 (
    .sw1(dipswitch_9_sw1), .sw2(dipswitch_9_sw2), .sw3(dipswitch_9_sw3), .sw4(dipswitch_9_sw4),
    .sw5(dipswitch_9_sw5), .sw6(dipswitch_9_sw6), .sw7(dipswitch_9_sw7), .sw8(dipswitch_9_sw8));
  DipSwitch dipswitch_10 (
    .sw1(dipswitch_10_sw1), .sw2(dipswitch_10_sw2), .sw3(dipswitch_10_sw3), .sw4(dipswitch_10_sw4),
    .sw5(dipswitch_10_sw5), .sw6(dipswitch_10_sw6), .sw7(dipswitch_10_sw7), .sw8(dipswitch_10_sw8));
  DipSwitch dipswitch_11 (
    .sw1(dipswitch_11_sw1), .sw2(dipswitch_11_sw2), .sw3(dipswitch_11_sw3), .sw4(dipswitch_11_sw4),
    .sw5(dipswitch_11_sw5), .sw6(dipswitch_11_sw6), .sw7(dipswitch_11_sw7), .sw8(dipswitch_11_sw8));
  DipSwitch dipswitch_12 (
    .sw1(dipswitch_12_sw1), .sw2(dipswitch_12_sw2), .sw3(dipswitch_12_sw3), .sw4(dipswitch_12_sw4),
    .sw5(dipswitch_12_sw5), .sw6(dipswitch_12_sw6), .sw7(dipswitch_12_sw7), .sw8(dipswitch_12_sw8));
  DipSwitch dipswitch_13 (
    .sw1(dipswitch_13_sw1), .sw2(dipswitch_13_sw2), .sw3(dipswitch_13_sw3), .sw4(dipswitch_13_sw4),
    .sw5(dipswitch_13_sw5), .sw6(dipswitch_13_sw6), .sw7(dipswitch_13_sw7), .sw8(dipswitch_13_sw8));
  DipSwitch dipswitch_14 (
    .sw1(dipswitch_14_sw1), .sw2(dipswitch_14_sw2), .sw3(dipswitch_14_sw3), .sw4(dipswitch_14_sw4),
    .sw5(dipswitch_14_sw5), .sw6(dipswitch_14_sw6), .sw7(dipswitch_14_sw7), .sw8(dipswitch_14_sw8));
  DipSwitch dipswitch_15 (
    .sw1(dipswitch_15_sw1), .sw2(dipswitch_15_sw2), .sw3(dipswitch_15_sw3), .sw4(dipswitch_15_sw4),
    .sw5(dipswitch_15_sw5), .sw6(dipswitch_15_sw6), .sw7(dipswitch_15_sw7), .sw8(dipswitch_15_sw8));
  DipSwitch dipswitch_16 (
    .sw1(dipswitch_16_sw1), .sw2(dipswitch_16_sw2), .sw3(dipswitch_16_sw3), .sw4(dipswitch_16_sw4),
    .sw5(dipswitch_16_sw5), .sw6(dipswitch_16_sw6), .sw7(dipswitch_16_sw7), .sw8(dipswitch_16_sw8));
  register_RAM h8 (
    .in_1(dipswitch_9_sw8), .in_2(dipswitch_9_sw7), .in_3(dipswitch_9_sw6), .in_4(dipswitch_9_sw5),
    .in_6(dipswitch_9_sw4), .in_7(dipswitch_9_sw3), .in_8(dipswitch_9_sw2), .in_9(dipswitch_9_sw1),
    .in_5(demultiplexer_1_out8[0]), .out_10(OUT1));
  register_RAM h9 (
    .in_1(dipswitch_10_sw8), .in_2(dipswitch_10_sw7), .in_3(dipswitch_10_sw6), .in_4(dipswitch_10_sw5),
    .in_6(dipswitch_10_sw4), .in_7(dipswitch_10_sw3), .in_8(dipswitch_10_sw2), .in_9(dipswitch_10_sw1),
    .in_5(demultiplexer_1_out8[1]), .out_10(OUT1));
  register_RAM h10 (
    .in_1(dipswitch_11_sw8), .in_2(dipswitch_11_sw7), .in_3(dipswitch_11_sw6), .in_4(dipswitch_11_sw5),
    .in_6(dipswitch_11_sw4), .in_7(dipswitch_11_sw3), .in_8(dipswitch_11_sw2), .in_9(dipswitch_11_sw1),
    .in_5(demultiplexer_1_out8[2]), .out_10(OUT1));
  register_RAM h11 (
    .in_1(dipswitch_12_sw8), .in_2(dipswitch_12_sw7), .in_3(dipswitch_12_sw6), .in_4(dipswitch_12_sw5),
    .in_6(dipswitch_12_sw4), .in_7(dipswitch_12_sw3), .in_8(dipswitch_12_sw2), .in_9(dipswitch_12_sw1),
    .in_5(demultiplexer_1_out8[3]), .out_10(OUT1));
  register_RAM h12 (
    .in_1(dipswitch_13_sw8), .in_2(dipswitch_13_sw7), .in_3(dipswitch_13_sw6), .in_4(dipswitch_13_sw5),
    .in_6(dipswitch_13_sw4), .in_7(dipswitch_13_sw3), .in_8(dipswitch_13_sw2), .in_9(dipswitch_13_sw1),
    .in_5(demultiplexer_1_out8[4]), .out_10(OUT1));
  register_RAM h13 (
    .in_1(dipswitch_14_sw8), .in_2(dipswitch_14_sw7), .in_3(dipswitch_14_sw6), .in_4(dipswitch_14_sw5),
    .in_6(dipswitch_14_sw4), .in_7(dipswitch_14_sw3), .in_8(dipswitch_14_sw2), .in_9(dipswitch_14_sw1),
    .in_5(demultiplexer_1_out8[5]), .out_10(OUT1));
  register_RAM h14 (
    .in_1(dipswitch_15_sw8), .in_2(dipswitch_15_sw7), .in_3(dipswitch_15_sw6), .in_4(dipswitch_15_sw5),
    .in_6(dipswitch_15_sw4), .in_7(dipswitch_15_sw3), .in_8(dipswitch_15_sw2), .in_9(dipswitch_15_sw1),
    .in_5(demultiplexer_1_out8[6]), .out_10(OUT1));
  register_RAM h15 (
    .in_1(dipswitch_16_sw8), .in_2(dipswitch_16_sw7), .in_3(dipswitch_16_sw6), .in_4(dipswitch_16_sw5),
    .in_6(dipswitch_16_sw4), .in_7(dipswitch_16_sw3), .in_8(dipswitch_16_sw2), .in_9(dipswitch_16_sw1),
    .in_5(demultiplexer_1_out8[7]), .out_10(OUT1));
endmodule

module IR (
  input  [7:0] in_1,
  input  CLR,
  input  CLK,
  input  Li,
  input  Ei,
  output [3:0] OUT_0a3,
  output [3:0] OUT_4a7
);

  wire [3:0] register_8bits_1_out_6;

  Register_8bits register_8bits_1 (
    .in_1(in_1), .Li(Li), .Ei(1'b1), .CLR(CLR), .CLK(CLK), .out_6({OUT_4a7, register_8bits_1_out_6}));
  assign OUT_0a3 = Ei ? register_8bits_1_out_6 : 4'bz;  // Controlled_Buffer controlled_buffer_1
endmodule

module register_RAM (
  input  in_1,
  input  in_2,
  input  in_3,
  input  in_4,
  input  in_5,
  input  in_6,
  input  in_7,
  input  in_8,
  input  in_9,
  output [7:0] out_10
);

  wire clock_1_out;

  Clock clock_1 (.out(clock_1_out));
  Register_8bits register_8bits_1 (
    .in_1({in_9, in_8, in_7, in_6, in_4, in_3, in_2, in_1}), .Li(1'b1), .Ei(in_5), .CLK(clock_1_out),
    .out_6(out_10));  // open: CLR
endmodule

module register_b (
  input  [7:0] in_1,
  input  CLK,
  input  LB,
  output [7:0] out_4
);

  Register_8bits register_8bits_1 (.in_1(in_1), .Li(LB), .Ei(1'b1), .CLK(CLK), .out_6(out_4));  // open: CLR
endmodule

module Acumulator (
  input  [7:0] in_1,
  input  CLK,
  input  LA,
  input  EA,
  output [7:0] free,
  output [7:0] out_6
);

  Register_8bits register_8bits_1 (.in_1(in_1), .Li(LA), .Ei(1'b1), .CLK(CLK), .out_6(free));  // open: CLR
  assign out_6 = EA ? free : 8'bz;  // Controlled_Buffer controlled_buffer_1
endmodule

module add_sub (
  input  Su,
  input  [7:0] INA,
  input  [7:0] INB,
  input  Eu,
  output [7:0] OUT1
);

  wire clock_1_out, not_1_out, sinal_1_out_4, xor_1_out;
  wire [7:0] inverter_1_out_3, inverter_2_out_3, inverter_3_out_3, register_8bits_1_out_6,
       somador_subtrator_8bits_1_s;

  Clock clock_1 (.out(clock_1_out));
  Register_8bits register_8bits_1 (
    .in_1(INA), .Li(not_1_out), .Ei(1'b1), .CLK(clock_1_out), .out_6(register_8bits_1_out_6));  // open: CLR
  not not_1 (not_1_out, Eu);
  ExactlyOne xor_1 (.out(xor_1_out), .in0(Su), .in1(register_8bits_1_out_6[7]), .in2(INB[7]));
  inverter inverter_1 (.in_1(register_8bits_1_out_6), .in_2(register_8bits_1_out_6[7]), .out_3(inverter_1_out_3));
  inverter inverter_2 (.in_1(INB), .in_2(INB[7]), .out_3(inverter_2_out_3));
  somador_subtrator_8bits somador_subtrator_8bits_1 (
    .A(inverter_1_out_3), .B(inverter_2_out_3), .Sub(xor_1_out), .S(somador_subtrator_8bits_1_s));  // open: Cout, Negative, Zero
  Sinal sinal_1 (.Sinal_A(register_8bits_1_out_6[7]), .Sinal_B(INB[7]), .Sinal_sub(xor_1_out), .out_4(sinal_1_out_4));
  inverter inverter_3 (.in_1(somador_subtrator_8bits_1_s), .in_2(sinal_1_out_4), .out_3(inverter_3_out_3));
  assign OUT1 = Eu ? inverter_3_out_3 : 8'bz;  // Controlled_Buffer controlled_buffer_1
endmodule

module controle (
  input  [3:0] in_1,
  input  CLK,
  input  Clear,
  output Ep,
  output Cp,
  output Li,
  output Su,
  output Lo,
  output Ea,
  output Lm,
  output Ce,
  output Ei,
  output La,
  output Lb,
  output Eu,
  output CLR,
  output [5:0] Timer
);

  wire and_2_out, and_3_out, and_4_out, and_5_out, and_6_out, and_7_out, and_8_out, and_9_out, and_10_out,
       and_11_out, and_12_out, and_13_out, and_14_out, and_15_out, and_16_out, and_17_out, decoder_1_1_out_3,
       decoder_1_1_out_4, decoder_1_1_out_6, decoder_1_1_out_7;

  Decoder_1 decoder_1_1 (
    .in_1(in_1), .in_2(Clear), .out_3(decoder_1_1_out_3), .out_4(decoder_1_1_out_4), .out_5(Su),
    .out_6(decoder_1_1_out_6), .out_7(decoder_1_1_out_7));
  Timer_6t timer_6t_1 (.CLK(CLK), .CLR(CLR), .T1(Ep), .T2(Cp), .T3(Li), .T4(Timer[3]), .T5(Timer[4]), .T6(Timer[5]));
  and and_1 (Ea, Timer[3], decoder_1_1_out_6);
  and and_2 (and_2_out, Timer[3], decoder_1_1_out_3);
  and and_3 (and_3_out, Timer[3], decoder_1_1_out_4);
  and and_4 (and_4_out, Timer[3], Su);
  and and_5 (and_5_out, Timer[4], decoder_1_1_out_3);
  and and_6 (and_6_out, Timer[4], decoder_1_1_out_4);
  and and_7 (and_7_out, Timer[4], Su);
  and and_8 (and_8_out, Timer[3], decoder_1_1_out_3);
  and and_9 (and_9_out, Timer[3], decoder_1_1_out_4);
  and and_10 (and_10_out, Timer[3], Su);
  and and_11 (and_11_out, Timer[4], decoder_1_1_out_3);
  and and_12 (and_12_out, Timer[5], decoder_1_1_out_4);
  and and_13 (and_13_out, Timer[5], Su);
  and and_14 (and_14_out, Timer[4], decoder_1_1_out_4);
  and and_15 (and_15_out, Timer[4], Su);
  and and_16 (and_16_out, Timer[5], decoder_1_1_out_4);
  and and_17 (and_17_out, Timer[5], Su);
  or or_1 (CLR, decoder_1_1_out_7, Clear);
  or or_2 (Lm, Ep, and_2_out, and_3_out, and_4_out);
  or or_3 (Ce, Li, and_5_out, and_6_out, and_7_out);
  or or_4 (Ei, and_8_out, and_9_out, and_10_out);
  or or_5 (La, and_11_out, and_12_out, and_13_out);
  or or_6 (Lb, and_14_out, and_15_out);
  or or_7 (Eu, and_16_out, and_17_out);

  assign Lo = Ea;
  assign Timer[2:0] = {Li, Cp, Ep};
endmodule

module Timer_6t (
  input  CLK,
  input  CLR,
  output T1,
  output T2,
  output T3,
  output T4,
  output T5,
  output T6
);

  wire not_1_out, not_2_out, undriven;

  not not_1 (not_1_out, undriven);
  D_Flip_Flop d_ff_1 (.D(T6), .clk(CLK), .Q(T1), .preset(CLR));  // open: Qn, reset
  not not_2 (not_2_out, not_1_out);
  D_Flip_Flop d_ff_2 (.D(T1), .clk(CLK), .Q(T2), .reset(CLR));  // open: Qn, preset
  // AND_Gate and_1 has open pins: in0=not_2_out, in1=not_1_out, out=open
  D_Flip_Flop d_ff_3 (.D(T2), .clk(CLK), .Q(T3), .reset(CLR));  // open: Qn, preset
  D_Flip_Flop d_ff_4 (.D(T3), .clk(CLK), .Q(T4), .reset(CLR));  // open: Qn, preset
  D_Flip_Flop d_ff_5 (.D(T4), .clk(CLK), .Q(T5), .reset(CLR));  // open: Qn, preset
  D_Flip_Flop d_ff_6 (.D(T5), .clk(CLK), .Q(T6), .reset(CLR));  // open: Qn, preset
endmodule

module Decoder_1 (
  input  [3:0] in_1,
  input  in_2,
  output out_3,
  output out_4,
  output out_5,
  output out_6,
  output out_7
);

  wire and_5_out;

  and and_1 (out_3, ~in_1[0], ~in_1[1], ~in_1[2], ~in_1[3]);  // AND_Gate
  and and_2 (out_4, in_1[0], ~in_1[1], ~in_1[2], ~in_1[3]);  // AND_Gate
  and and_3 (out_5, ~in_1[0], in_1[1], ~in_1[2], ~in_1[3]);  // AND_Gate
  and and_4 (out_6, ~in_1[0], in_1[1], in_1[2], in_1[3]);  // AND_Gate
  and and_5 (and_5_out, in_1[0], in_1[1], in_1[2], in_1[3]);
  J_K_Flip_Flop j_k_ff_1 (.Q(out_7), .preset(and_5_out), .reset(in_2));  // open: J, K, clk, Qn
endmodule

module Register_IR (
  input  [7:0] in_1,
  input  Li,
  input  Ei,
  input  CLR,
  input  CLK,
  output [7:0] out_6
);

  wire controlled_buffer_1_out, controlled_buffer_2_out, controlled_buffer_3_out, controlled_buffer_4_out,
       controlled_buffer_5_out, controlled_buffer_6_out, controlled_buffer_7_out, controlled_buffer_8_out,
       d_ff_1_q, d_ff_2_q, d_ff_3_q, d_ff_4_q;

  D_Flip_Flop #(.trigger("high")) d_ff_1 (
    .D(controlled_buffer_1_out), .clk(CLK), .Q(d_ff_1_q), .reset(CLR));  // open: Qn, preset
  assign controlled_buffer_1_out = Li ? in_1[0] : 1'bz;  // Controlled_Buffer controlled_buffer_1
  D_Flip_Flop #(.trigger("high")) d_ff_2 (
    .D(controlled_buffer_2_out), .clk(CLK), .Q(d_ff_2_q), .reset(CLR));  // open: Qn, preset
  assign controlled_buffer_2_out = Li ? in_1[1] : 1'bz;  // Controlled_Buffer controlled_buffer_2
  D_Flip_Flop #(.trigger("high")) d_ff_3 (
    .D(controlled_buffer_3_out), .clk(CLK), .Q(d_ff_3_q), .reset(CLR));  // open: Qn, preset
  assign controlled_buffer_3_out = Li ? in_1[2] : 1'bz;  // Controlled_Buffer controlled_buffer_3
  D_Flip_Flop #(.trigger("high")) d_ff_4 (
    .D(controlled_buffer_4_out), .clk(CLK), .Q(d_ff_4_q), .reset(CLR));  // open: Qn, preset
  assign controlled_buffer_4_out = Li ? in_1[3] : 1'bz;  // Controlled_Buffer controlled_buffer_4
  D_Flip_Flop #(.trigger("high")) d_ff_5 (
    .D(controlled_buffer_5_out), .clk(CLK), .Q(out_6[4]), .reset(CLR));  // open: Qn, preset
  assign controlled_buffer_5_out = Li ? in_1[4] : 1'bz;  // Controlled_Buffer controlled_buffer_5
  D_Flip_Flop #(.trigger("high")) d_ff_6 (
    .D(controlled_buffer_6_out), .clk(CLK), .Q(out_6[5]), .reset(CLR));  // open: Qn, preset
  assign controlled_buffer_6_out = Li ? in_1[5] : 1'bz;  // Controlled_Buffer controlled_buffer_6
  D_Flip_Flop #(.trigger("high")) d_ff_7 (
    .D(controlled_buffer_7_out), .clk(CLK), .Q(out_6[6]), .reset(CLR));  // open: Qn, preset
  assign controlled_buffer_7_out = Li ? in_1[6] : 1'bz;  // Controlled_Buffer controlled_buffer_7
  D_Flip_Flop #(.trigger("high")) d_ff_8 (
    .D(controlled_buffer_8_out), .clk(CLK), .Q(out_6[7]), .reset(CLR));  // open: Qn, preset
  assign controlled_buffer_8_out = Li ? in_1[7] : 1'bz;  // Controlled_Buffer controlled_buffer_8
  assign out_6[0] = Ei ? d_ff_1_q : 1'bz;  // Controlled_Buffer controlled_buffer_9
  assign out_6[1] = Ei ? d_ff_2_q : 1'bz;  // Controlled_Buffer controlled_buffer_10
  assign out_6[2] = Ei ? d_ff_3_q : 1'bz;  // Controlled_Buffer controlled_buffer_11
  assign out_6[3] = Ei ? d_ff_4_q : 1'bz;  // Controlled_Buffer controlled_buffer_12
endmodule

module somador_1bit (
  input  A,
  input  B,
  input  Cin,
  output Cout,
  output Soma
);

  wire and_1_out, and_2_out, and_3_out, and_4_out, and_5_out, xnor_1_out, xor_1_out;

  and and_1 (and_1_out, A, B);
  and and_2 (and_2_out, A, Cin);
  and and_3 (and_3_out, B, Cin);
  xnor xnor_1 (xnor_1_out, A, B);
  xor xor_1 (xor_1_out, A, B);
  or or_1 (Cout, and_1_out, and_2_out, and_3_out);
  and and_4 (and_4_out, xnor_1_out, Cin);
  and and_5 (and_5_out, xor_1_out, ~Cin);  // AND_Gate
  or or_2 (Soma, and_4_out, and_5_out);
endmodule

module somador_subtrator_1bit (
  input  Cin,
  input  Sub,
  input  A,
  input  B,
  output S,
  output Cout
);

  wire xor_1_out;

  xor xor_1 (xor_1_out, Sub, B);
  somador_1bit somador_1bit_1 (.A(A), .B(xor_1_out), .Cin(Cin), .Cout(Cout), .Soma(S));
endmodule

module somador_subtrator_8bits (
  input  Sub,
  input  [7:0] A,
  input  [7:0] B,
  output [7:0] S,
  output Zero,
  output Negative,
  output Cout
);

  wire somador_subtrator_1bit_1_cout, somador_subtrator_1bit_2_cout, somador_subtrator_1bit_3_cout,
       somador_subtrator_1bit_4_cout, somador_subtrator_1bit_5_cout, somador_subtrator_1bit_6_cout,
       somador_subtrator_1bit_7_cout;

  somador_subtrator_1bit somador_subtrator_1bit_1 (
    .A(A[0]), .B(B[0]), .Sub(Sub), .Cin(Sub), .Cout(somador_subtrator_1bit_1_cout), .S(S[0]));
  somador_subtrator_1bit somador_subtrator_1bit_2 (
    .A(A[1]), .B(B[1]), .Sub(Sub), .Cin(somador_subtrator_1bit_1_cout), .Cout(somador_subtrator_1bit_2_cout),
    .S(S[1]));
  somador_subtrator_1bit somador_subtrator_1bit_3 (
    .A(A[2]), .B(B[2]), .Sub(Sub), .Cin(somador_subtrator_1bit_2_cout), .Cout(somador_subtrator_1bit_3_cout),
    .S(S[2]));
  somador_subtrator_1bit somador_subtrator_1bit_4 (
    .A(A[3]), .B(B[3]), .Sub(Sub), .Cin(somador_subtrator_1bit_3_cout), .Cout(somador_subtrator_1bit_4_cout),
    .S(S[3]));
  somador_subtrator_1bit somador_subtrator_1bit_5 (
    .A(A[4]), .B(B[4]), .Sub(Sub), .Cin(somador_subtrator_1bit_4_cout), .Cout(somador_subtrator_1bit_5_cout),
    .S(S[4]));
  somador_subtrator_1bit somador_subtrator_1bit_6 (
    .A(A[5]), .B(B[5]), .Sub(Sub), .Cin(somador_subtrator_1bit_5_cout), .Cout(somador_subtrator_1bit_6_cout),
    .S(S[5]));
  somador_subtrator_1bit somador_subtrator_1bit_7 (
    .A(A[6]), .B(B[6]), .Sub(Sub), .Cin(somador_subtrator_1bit_6_cout), .Cout(somador_subtrator_1bit_7_cout),
    .S(S[6]));
  somador_subtrator_1bit somador_subtrator_1bit_8 (
    .A(A[7]), .B(B[7]), .Sub(Sub), .Cin(somador_subtrator_1bit_7_cout), .Cout(Cout), .S(Negative));
  and and_1 (Zero, ~S[0], ~S[1], ~S[2], ~S[3], ~S[4], ~S[5], ~S[6]);  // AND_Gate

  assign S[7] = Negative;
endmodule

module saida (
  input  [7:0] in_1,
  input  CLR,
  input  Lo,
  output sinal,
  output [3:0] out_5,
  output [3:0] out_6,
  output [3:0] out_7
);

  wire clock_1_out, or_1_out, s_r_ff_1_q;
  wire [3:0] binary_to_bcd_converter_1_p2, binary_to_bcd_converter_1_p3, binary_to_bcd_converter_1_p4;
  wire [6:0] register_8bits_1_out_6;
  wire [7:0] controlled_buffer_1_out, inverter_1_out_3;

  Clock clock_1 (.out(clock_1_out));
  or or_1 (or_1_out, CLR, Lo);
  S_R_Flip_Flop #(.trigger("high")) s_r_ff_1 (.Q(s_r_ff_1_q), .preset(or_1_out));  // open: S, R, clk, reset, Qn
  Register_8bits register_8bits_1 (
    .in_1(in_1), .Li(Lo), .Ei(s_r_ff_1_q), .CLR(CLR), .CLK(clock_1_out),
    .out_6({sinal, register_8bits_1_out_6}));
  inverter inverter_1 (.in_1({sinal, register_8bits_1_out_6}), .in_2(sinal), .out_3(inverter_1_out_3));
  assign controlled_buffer_1_out = s_r_ff_1_q ? inverter_1_out_3 : 8'bz;  // Controlled_Buffer controlled_buffer_1
  // Binary_to_BCD_converter binary_to_bcd_converter_1: pin names not known; wires that end beside it: {1'b0, controlled_buffer_1_out}, binary_to_bcd_converter_1_p2, binary_to_bcd_converter_1_p3, binary_to_bcd_converter_1_p4
  assign out_5 = s_r_ff_1_q ? binary_to_bcd_converter_1_p2 : 4'bz;  // Controlled_Buffer controlled_buffer_2
  assign out_6 = s_r_ff_1_q ? binary_to_bcd_converter_1_p3 : 4'bz;  // Controlled_Buffer controlled_buffer_3
  assign out_7 = s_r_ff_1_q ? binary_to_bcd_converter_1_p4 : 4'bz;  // Controlled_Buffer controlled_buffer_4
endmodule

module inverter (
  input  [7:0] in_1,
  input  in_2,
  output [7:0] out_3
);

  wire [7:0] negator_1_out;

  Negator negator_1 (.in(in_1), .out(negator_1_out));
  Multiplexer #(.width(8)) multiplexer_1 (.in0(in_1), .in1(negator_1_out), .out(out_3), .sel(in_2));
endmodule

module Sinal (
  input  Sinal_A,
  input  Sinal_B,
  input  Sinal_sub,
  output out_4
);

  wire xor_1_out;

  xor xor_1 (xor_1_out, Sinal_B, Sinal_sub);
  and and_1 (out_4, Sinal_A, xor_1_out);
endmodule

module display_out (
  input  [3:0] in_1,
  input  in_2,
  output [6:0] ZERO,
  output [6:0] ZERO1,
  output [6:0] out_5,
  output [6:0] out_6,
  output [6:0] out_7,
  output [6:0] out_8,
  output [6:0] out_9,
  output [6:0] out_10,
  output [6:0] out_11,
  output [6:0] out_12,
  output [6:0] out_13,
  output [6:0] out_14,
  output [6:0] out_15,
  output [6:0] out_16,
  output [6:0] out_17,
  output [6:0] out_18,
  output [6:0] out_19
);

  wire decoder_1_1_out_3;
  wire [0:0] and_1_out;
  wire [3:3] decoder_1_1_out_7;
  wire [5:5] decoder_1_1_out_4, decoder_1_1_out_5;
  wire [6:6] decoder_1_1_out_6;

  Decoder_1 decoder_1_1 (
    .in_1(in_1), .in_2(in_2), .out_3(decoder_1_1_out_3), .out_4(decoder_1_1_out_4[5]),
    .out_5(decoder_1_1_out_5[5]), .out_6(decoder_1_1_out_6[6]), .out_7(decoder_1_1_out_7[3]));
  and and_1 (and_1_out[0], ~decoder_1_1_out_7[3], decoder_1_1_out_3);  // AND_Gate
  assign out_5 = and_1_out[0] ? {7{and_1_out[0]}} : 7'bz;  // Controlled_Buffer controlled_buffer_1
  assign out_5 = decoder_1_1_out_4[5] ? {1'b0, {6{decoder_1_1_out_4[5]}}} : 7'bz;  // Controlled_Buffer controlled_buffer_2
  assign out_5 = decoder_1_1_out_5[5] ? {1'b0, {2{decoder_1_1_out_5[5]}}, 2'b00, decoder_1_1_out_5[5], 1'b0} : 7'bz;  // Controlled_Buffer controlled_buffer_3
  assign out_5 = decoder_1_1_out_6[6] ? {1'b0, {5{decoder_1_1_out_6[6]}}, 1'b0} : 7'bz;  // Controlled_Buffer controlled_buffer_4
  assign out_5 = decoder_1_1_out_7[3] ? {7{decoder_1_1_out_7[3]}} : 7'bz;  // Controlled_Buffer controlled_buffer_5
  assign out_6 = and_1_out[0] ? {{6{1'b0}}, and_1_out[0]} : 7'bz;  // Controlled_Buffer controlled_buffer_6
  assign out_6 = decoder_1_1_out_4[5] ? {decoder_1_1_out_4[5], 2'b00, decoder_1_1_out_4[5], 3'b000} : 7'bz;  // Controlled_Buffer controlled_buffer_7
  assign out_6 = decoder_1_1_out_5[5] ? {decoder_1_1_out_5[5], 2'b00, decoder_1_1_out_5[5], 2'b00, decoder_1_1_out_5[5]} : 7'bz;  // Controlled_Buffer controlled_buffer_8
  assign out_6 = decoder_1_1_out_6[6] ? {decoder_1_1_out_6[6], {5{1'b0}}, decoder_1_1_out_6[6]} : 7'bz;  // Controlled_Buffer controlled_buffer_9
  assign out_6 = decoder_1_1_out_7[3] ? {3'b000, decoder_1_1_out_7[3], 3'b000} : 7'bz;  // Controlled_Buffer controlled_buffer_10
  assign out_7 = and_1_out[0] ? {{6{1'b0}}, and_1_out[0]} : 7'bz;  // Controlled_Buffer controlled_buffer_11
  assign out_7 = decoder_1_1_out_4[5] ? {decoder_1_1_out_4[5], 2'b00, decoder_1_1_out_4[5], 3'b000} : 7'bz;  // Controlled_Buffer controlled_buffer_12
  assign out_7 = decoder_1_1_out_5[5] ? {decoder_1_1_out_5[5], 2'b00, decoder_1_1_out_5[5], 2'b00, decoder_1_1_out_5[5]} : 7'bz;  // Controlled_Buffer controlled_buffer_13
  assign out_7 = decoder_1_1_out_6[6] ? {decoder_1_1_out_6[6], {5{1'b0}}, decoder_1_1_out_6[6]} : 7'bz;  // Controlled_Buffer controlled_buffer_14
  assign out_7 = decoder_1_1_out_7[3] ? {3'b000, decoder_1_1_out_7[3], 3'b000} : 7'bz;  // Controlled_Buffer controlled_buffer_15
  assign out_8 = and_1_out[0] ? {{6{1'b0}}, and_1_out[0]} : 7'bz;  // Controlled_Buffer controlled_buffer_16
  assign out_8 = decoder_1_1_out_4[5] ? {decoder_1_1_out_4[5], 2'b00, decoder_1_1_out_4[5], 3'b000} : 7'bz;  // Controlled_Buffer controlled_buffer_17
  assign out_8 = decoder_1_1_out_5[5] ? {decoder_1_1_out_5[5], 2'b00, decoder_1_1_out_5[5], 2'b00, decoder_1_1_out_5[5]} : 7'bz;  // Controlled_Buffer controlled_buffer_18
  assign out_8 = decoder_1_1_out_6[6] ? {decoder_1_1_out_6[6], {5{1'b0}}, decoder_1_1_out_6[6]} : 7'bz;  // Controlled_Buffer controlled_buffer_19
  assign out_8 = decoder_1_1_out_7[3] ? {3'b000, decoder_1_1_out_7[3], 3'b000} : 7'bz;  // Controlled_Buffer controlled_buffer_20
  assign out_9 = and_1_out[0] ? {{6{1'b0}}, and_1_out[0]} : 7'bz;  // Controlled_Buffer controlled_buffer_21
  assign out_9 = decoder_1_1_out_4[5] ? {1'b0, {6{decoder_1_1_out_4[5]}}} : 7'bz;  // Controlled_Buffer controlled_buffer_22
  assign out_9 = decoder_1_1_out_5[5] ? {1'b0, decoder_1_1_out_5[5], 2'b00, {2{decoder_1_1_out_5[5]}}, 1'b0} : 7'bz;  // Controlled_Buffer controlled_buffer_23
  assign out_9 = decoder_1_1_out_6[6] ? {1'b0, {5{decoder_1_1_out_6[6]}}, 1'b0} : 7'bz;  // Controlled_Buffer controlled_buffer_24
  assign out_9 = decoder_1_1_out_7[3] ? {7{decoder_1_1_out_7[3]}} : 7'bz;  // Controlled_Buffer controlled_buffer_25
  assign out_10 = and_1_out[0] ? {7{and_1_out[0]}} : 7'bz;  // Controlled_Buffer controlled_buffer_26
  assign out_10 = decoder_1_1_out_4[5] ? {7{decoder_1_1_out_4[5]}} : 7'bz;  // Controlled_Buffer controlled_buffer_27
  assign out_10 = decoder_1_1_out_5[5] ? {{6{decoder_1_1_out_5[5]}}, 1'b0} : 7'bz;  // Controlled_Buffer controlled_buffer_28
  assign out_10 = decoder_1_1_out_6[6] ? {{6{decoder_1_1_out_6[6]}}, 1'b0} : 7'bz;  // Controlled_Buffer controlled_buffer_29
  assign out_10 = decoder_1_1_out_7[3] ? {7{decoder_1_1_out_7[3]}} : 7'bz;  // Controlled_Buffer controlled_buffer_30
  assign out_11 = and_1_out[0] ? {and_1_out[0], {5{1'b0}}, and_1_out[0]} : 7'bz;  // Controlled_Buffer controlled_buffer_31
  assign out_11 = decoder_1_1_out_4[5] ? {decoder_1_1_out_4[5], {5{1'b0}}, decoder_1_1_out_4[5]} : 7'bz;  // Controlled_Buffer controlled_buffer_32
  assign out_11 = decoder_1_1_out_5[5] ? {{6{1'b0}}, decoder_1_1_out_5[5]} : 7'bz;  // Controlled_Buffer controlled_buffer_33
  assign out_11 = decoder_1_1_out_6[6] ? {{6{1'b0}}, decoder_1_1_out_6[6]} : 7'bz;  // Controlled_Buffer controlled_buffer_34
  assign out_11 = decoder_1_1_out_7[3] ? {{6{1'b0}}, decoder_1_1_out_7[3]} : 7'bz;  // Controlled_Buffer controlled_buffer_35
  assign out_12 = and_1_out[0] ? {and_1_out[0], {5{1'b0}}, and_1_out[0]} : 7'bz;  // Controlled_Buffer controlled_buffer_36
  assign out_12 = decoder_1_1_out_4[5] ? {decoder_1_1_out_4[5], {5{1'b0}}, decoder_1_1_out_4[5]} : 7'bz;  // Controlled_Buffer controlled_buffer_37
  assign out_12 = decoder_1_1_out_5[5] ? {{6{1'b0}}, decoder_1_1_out_5[5]} : 7'bz;  // Controlled_Buffer controlled_buffer_38
  assign out_12 = decoder_1_1_out_6[6] ? {{6{1'b0}}, decoder_1_1_out_6[6]} : 7'bz;  // Controlled_Buffer controlled_buffer_39
  assign out_12 = decoder_1_1_out_7[3] ? {{6{1'b0}}, decoder_1_1_out_7[3]} : 7'bz;  // Controlled_Buffer controlled_buffer_40
  assign out_13 = and_1_out[0] ? {and_1_out[0], {5{1'b0}}, and_1_out[0]} : 7'bz;  // Controlled_Buffer controlled_buffer_41
  assign out_13 = decoder_1_1_out_4[5] ? {decoder_1_1_out_4[5], {5{1'b0}}, decoder_1_1_out_4[5]} : 7'bz;  // Controlled_Buffer controlled_buffer_42
  assign out_13 = decoder_1_1_out_5[5] ? {{6{1'b0}}, decoder_1_1_out_5[5]} : 7'bz;  // Controlled_Buffer controlled_buffer_43
  assign out_13 = decoder_1_1_out_6[6] ? {{6{1'b0}}, decoder_1_1_out_6[6]} : 7'bz;  // Controlled_Buffer controlled_buffer_44
  assign out_13 = decoder_1_1_out_7[3] ? {{6{1'b0}}, decoder_1_1_out_7[3]} : 7'bz;  // Controlled_Buffer controlled_buffer_45
  assign out_14 = and_1_out[0] ? {1'b0, {5{and_1_out[0]}}, 1'b0} : 7'bz;  // Controlled_Buffer controlled_buffer_46
  assign out_14 = decoder_1_1_out_4[5] ? {1'b0, {5{decoder_1_1_out_4[5]}}, 1'b0} : 7'bz;  // Controlled_Buffer controlled_buffer_47
  assign out_14 = decoder_1_1_out_5[5] ? {{6{decoder_1_1_out_5[5]}}, 1'b0} : 7'bz;  // Controlled_Buffer controlled_buffer_48
  assign out_14 = decoder_1_1_out_6[6] ? {{6{decoder_1_1_out_6[6]}}, 1'b0} : 7'bz;  // Controlled_Buffer controlled_buffer_49
  assign out_14 = decoder_1_1_out_7[3] ? {{6{1'b0}}, decoder_1_1_out_7[3]} : 7'bz;  // Controlled_Buffer controlled_buffer_50
  assign out_15 = and_1_out[0] ? {1'b0, {6{and_1_out[0]}}} : 7'bz;  // Controlled_Buffer controlled_buffer_51
  assign out_15 = decoder_1_1_out_4[5] ? {7{decoder_1_1_out_4[5]}} : 7'bz;  // Controlled_Buffer controlled_buffer_52
  assign out_15 = decoder_1_1_out_5[5] ? {7{decoder_1_1_out_5[5]}} : 7'bz;  // Controlled_Buffer controlled_buffer_53
  assign out_15 = decoder_1_1_out_6[6] ? {decoder_1_1_out_6[6], {6{1'b0}}} : 7'bz;  // Controlled_Buffer controlled_buffer_54
  assign out_15 = decoder_1_1_out_7[3] ? {decoder_1_1_out_7[3], {6{1'b0}}} : 7'bz;  // Controlled_Buffer controlled_buffer_55
  assign out_16 = and_1_out[0] ? {and_1_out[0], 2'b00, and_1_out[0], 3'b000} : 7'bz;  // Controlled_Buffer controlled_buffer_56
  assign out_16 = decoder_1_1_out_4[5] ? {decoder_1_1_out_4[5], {5{1'b0}}, decoder_1_1_out_4[5]} : 7'bz;  // Controlled_Buffer controlled_buffer_57
  assign out_16 = decoder_1_1_out_5[5] ? {decoder_1_1_out_5[5], 2'b00, decoder_1_1_out_5[5], 2'b00, decoder_1_1_out_5[5]} : 7'bz;  // Controlled_Buffer controlled_buffer_58
  assign out_16 = decoder_1_1_out_6[6] ? {decoder_1_1_out_6[6], {6{1'b0}}} : 7'bz;  // Controlled_Buffer controlled_buffer_59
  assign out_16 = decoder_1_1_out_7[3] ? {decoder_1_1_out_7[3], {6{1'b0}}} : 7'bz;  // Controlled_Buffer controlled_buffer_60
  assign out_17 = and_1_out[0] ? {and_1_out[0], 2'b00, and_1_out[0], 3'b000} : 7'bz;  // Controlled_Buffer controlled_buffer_61
  assign out_17 = decoder_1_1_out_4[5] ? {decoder_1_1_out_4[5], {5{1'b0}}, decoder_1_1_out_4[5]} : 7'bz;  // Controlled_Buffer controlled_buffer_62
  assign out_17 = decoder_1_1_out_5[5] ? {decoder_1_1_out_5[5], 2'b00, decoder_1_1_out_5[5], 2'b00, decoder_1_1_out_5[5]} : 7'bz;  // Controlled_Buffer controlled_buffer_63
  assign out_17 = decoder_1_1_out_6[6] ? {7{decoder_1_1_out_6[6]}} : 7'bz;  // Controlled_Buffer controlled_buffer_64
  assign out_17 = decoder_1_1_out_7[3] ? {7{decoder_1_1_out_7[3]}} : 7'bz;  // Controlled_Buffer controlled_buffer_65
  assign out_18 = and_1_out[0] ? {and_1_out[0], 2'b00, and_1_out[0], 3'b000} : 7'bz;  // Controlled_Buffer controlled_buffer_66
  assign out_18 = decoder_1_1_out_4[5] ? {decoder_1_1_out_4[5], {5{1'b0}}, decoder_1_1_out_4[5]} : 7'bz;  // Controlled_Buffer controlled_buffer_67
  assign out_18 = decoder_1_1_out_5[5] ? {decoder_1_1_out_5[5], 2'b00, decoder_1_1_out_5[5], 2'b00, decoder_1_1_out_5[5]} : 7'bz;  // Controlled_Buffer controlled_buffer_68
  assign out_18 = decoder_1_1_out_6[6] ? {decoder_1_1_out_6[6], {6{1'b0}}} : 7'bz;  // Controlled_Buffer controlled_buffer_69
  assign out_18 = decoder_1_1_out_7[3] ? {decoder_1_1_out_7[3], {6{1'b0}}} : 7'bz;  // Controlled_Buffer controlled_buffer_70
  assign out_19 = and_1_out[0] ? {1'b0, {6{and_1_out[0]}}} : 7'bz;  // Controlled_Buffer controlled_buffer_71
  assign out_19 = decoder_1_1_out_4[5] ? {1'b0, {5{decoder_1_1_out_4[5]}}, 1'b0} : 7'bz;  // Controlled_Buffer controlled_buffer_72
  assign out_19 = decoder_1_1_out_5[5] ? {1'b0, {2{decoder_1_1_out_5[5]}}, 1'b0, {2{decoder_1_1_out_5[5]}}, 1'b0} : 7'bz;  // Controlled_Buffer controlled_buffer_73
  assign out_19 = decoder_1_1_out_6[6] ? {decoder_1_1_out_6[6], {6{1'b0}}} : 7'bz;  // Controlled_Buffer controlled_buffer_74
  assign out_19 = decoder_1_1_out_7[3] ? {decoder_1_1_out_7[3], {6{1'b0}}} : 7'bz;  // Controlled_Buffer controlled_buffer_75

  assign ZERO = {7{1'b0}};
  assign ZERO1 = {7{1'b0}};
endmodule

module registrador_16bits (
  input  [15:0] ENTRADA,
  input  Li,
  input  Ei,
  input  CLR,
  input  CLK,
  output [15:0] SAIDA
);

  wire controlled_buffer_1_out, controlled_buffer_2_out, controlled_buffer_3_out, controlled_buffer_4_out,
       controlled_buffer_5_out, controlled_buffer_6_out, controlled_buffer_7_out, controlled_buffer_8_out,
       controlled_buffer_9_out, controlled_buffer_10_out, controlled_buffer_11_out, controlled_buffer_12_out,
       controlled_buffer_13_out, controlled_buffer_14_out, controlled_buffer_15_out,
       controlled_buffer_16_out, d_ff_1_q, d_ff_2_q, d_ff_3_q, d_ff_4_q, d_ff_5_q, d_ff_6_q, d_ff_7_q,
       d_ff_8_q, d_ff_9_q, d_ff_10_q, d_ff_11_q, d_ff_12_q, d_ff_13_q, d_ff_14_q, d_ff_15_q, d_ff_16_q;

  assign controlled_buffer_1_out = Li ? ENTRADA[0] : 1'bz;  // Controlled_Buffer controlled_buffer_1
  assign controlled_buffer_2_out = Li ? ENTRADA[1] : 1'bz;  // Controlled_Buffer controlled_buffer_2
  assign controlled_buffer_3_out = Li ? ENTRADA[2] : 1'bz;  // Controlled_Buffer controlled_buffer_3
  assign controlled_buffer_4_out = Li ? ENTRADA[3] : 1'bz;  // Controlled_Buffer controlled_buffer_4
  assign controlled_buffer_5_out = Li ? ENTRADA[4] : 1'bz;  // Controlled_Buffer controlled_buffer_5
  assign controlled_buffer_6_out = Li ? ENTRADA[5] : 1'bz;  // Controlled_Buffer controlled_buffer_6
  assign controlled_buffer_7_out = Li ? ENTRADA[6] : 1'bz;  // Controlled_Buffer controlled_buffer_7
  assign controlled_buffer_8_out = Li ? ENTRADA[7] : 1'bz;  // Controlled_Buffer controlled_buffer_8
  assign controlled_buffer_9_out = Li ? ENTRADA[8] : 1'bz;  // Controlled_Buffer controlled_buffer_9
  assign controlled_buffer_10_out = Li ? ENTRADA[9] : 1'bz;  // Controlled_Buffer controlled_buffer_10
  assign controlled_buffer_11_out = Li ? ENTRADA[10] : 1'bz;  // Controlled_Buffer controlled_buffer_11
  assign controlled_buffer_12_out = Li ? ENTRADA[11] : 1'bz;  // Controlled_Buffer controlled_buffer_12
  assign controlled_buffer_13_out = Li ? ENTRADA[12] : 1'bz;  // Controlled_Buffer controlled_buffer_13
  assign controlled_buffer_14_out = Li ? ENTRADA[13] : 1'bz;  // Controlled_Buffer controlled_buffer_14
  assign controlled_buffer_15_out = Li ? ENTRADA[14] : 1'bz;  // Controlled_Buffer controlled_buffer_15
  assign controlled_buffer_16_out = Li ? ENTRADA[15] : 1'bz;  // Controlled_Buffer controlled_buffer_16
  D_Flip_Flop #(.trigger("high")) d_ff_1 (
    .D(controlled_buffer_1_out), .clk(CLK), .Q(d_ff_1_q), .reset(CLR));  // open: Qn, preset
  D_Flip_Flop #(.trigger("high")) d_ff_2 (
    .D(controlled_buffer_2_out), .clk(CLK), .Q(d_ff_2_q), .reset(CLR));  // open: Qn, preset
  D_Flip_Flop #(.trigger("high")) d_ff_3 (
    .D(controlled_buffer_3_out), .clk(CLK), .Q(d_ff_3_q), .reset(CLR));  // open: Qn, preset
  D_Flip_Flop #(.trigger("high")) d_ff_4 (
    .D(controlled_buffer_4_out), .clk(CLK), .Q(d_ff_4_q), .reset(CLR));  // open: Qn, preset
  D_Flip_Flop #(.trigger("high")) d_ff_5 (
    .D(controlled_buffer_5_out), .clk(CLK), .Q(d_ff_5_q), .reset(CLR));  // open: Qn, preset
  D_Flip_Flop #(.trigger("high")) d_ff_6 (
    .D(controlled_buffer_6_out), .clk(CLK), .Q(d_ff_6_q), .reset(CLR));  // open: Qn, preset
  D_Flip_Flop #(.trigger("high")) d_ff_7 (
    .D(controlled_buffer_7_out), .clk(CLK), .Q(d_ff_7_q), .reset(CLR));  // open: Qn, preset
  D_Flip_Flop #(.trigger("high")) d_ff_8 (
    .D(controlled_buffer_8_out), .clk(CLK), .Q(d_ff_8_q), .reset(CLR));  // open: Qn, preset
  D_Flip_Flop #(.trigger("high")) d_ff_9 (
    .D(controlled_buffer_9_out), .clk(CLK), .Q(d_ff_9_q), .reset(CLR));  // open: Qn, preset
  D_Flip_Flop #(.trigger("high")) d_ff_10 (
    .D(controlled_buffer_10_out), .clk(CLK), .Q(d_ff_10_q), .reset(CLR));  // open: Qn, preset
  D_Flip_Flop #(.trigger("high")) d_ff_11 (
    .D(controlled_buffer_11_out), .clk(CLK), .Q(d_ff_11_q), .reset(CLR));  // open: Qn, preset
  D_Flip_Flop #(.trigger("high")) d_ff_12 (
    .D(controlled_buffer_12_out), .clk(CLK), .Q(d_ff_12_q), .reset(CLR));  // open: Qn, preset
  D_Flip_Flop #(.trigger("high")) d_ff_13 (
    .D(controlled_buffer_13_out), .clk(CLK), .Q(d_ff_13_q), .reset(CLR));  // open: Qn, preset
  D_Flip_Flop #(.trigger("high")) d_ff_14 (
    .D(controlled_buffer_14_out), .clk(CLK), .Q(d_ff_14_q), .reset(CLR));  // open: Qn, preset
  D_Flip_Flop #(.trigger("high")) d_ff_15 (
    .D(controlled_buffer_15_out), .clk(CLK), .Q(d_ff_15_q), .reset(CLR));  // open: Qn, preset
  D_Flip_Flop #(.trigger("high")) d_ff_16 (
    .D(controlled_buffer_16_out), .clk(CLK), .Q(d_ff_16_q), .reset(CLR));  // open: Qn, preset
  assign SAIDA[0] = Ei ? d_ff_1_q : 1'bz;  // Controlled_Buffer controlled_buffer_17
  assign SAIDA[1] = Ei ? d_ff_2_q : 1'bz;  // Controlled_Buffer controlled_buffer_18
  assign SAIDA[2] = Ei ? d_ff_3_q : 1'bz;  // Controlled_Buffer controlled_buffer_19
  assign SAIDA[3] = Ei ? d_ff_4_q : 1'bz;  // Controlled_Buffer controlled_buffer_20
  assign SAIDA[4] = Ei ? d_ff_5_q : 1'bz;  // Controlled_Buffer controlled_buffer_21
  assign SAIDA[5] = Ei ? d_ff_6_q : 1'bz;  // Controlled_Buffer controlled_buffer_22
  assign SAIDA[6] = Ei ? d_ff_7_q : 1'bz;  // Controlled_Buffer controlled_buffer_23
  assign SAIDA[7] = Ei ? d_ff_8_q : 1'bz;  // Controlled_Buffer controlled_buffer_24
  assign SAIDA[8] = Ei ? d_ff_9_q : 1'bz;  // Controlled_Buffer controlled_buffer_25
  assign SAIDA[9] = Ei ? d_ff_10_q : 1'bz;  // Controlled_Buffer controlled_buffer_26
  assign SAIDA[10] = Ei ? d_ff_11_q : 1'bz;  // Controlled_Buffer controlled_buffer_27
  assign SAIDA[11] = Ei ? d_ff_12_q : 1'bz;  // Controlled_Buffer controlled_buffer_28
  assign SAIDA[12] = Ei ? d_ff_13_q : 1'bz;  // Controlled_Buffer controlled_buffer_29
  assign SAIDA[13] = Ei ? d_ff_14_q : 1'bz;  // Controlled_Buffer controlled_buffer_30
  assign SAIDA[14] = Ei ? d_ff_15_q : 1'bz;  // Controlled_Buffer controlled_buffer_31
  assign SAIDA[15] = Ei ? d_ff_16_q : 1'bz;  // Controlled_Buffer controlled_buffer_32
endmodule

module REGISTRADOR_DE_16BIT (
);

  registrador_16bits registrador_16bits_1 ();  // open: ENTRADA, Li, Ei, CLR, CLK, SAIDA
endmodule
