// Logisim project TrabalhodeMicroprocessador.circ as structural Verilog
module main (
  input  [15:0] IN0,
  input  write0,
  input  read0,
  input  [15:0] IN1,
  input  [3:0] in_5,
  input  Write1,
  input  Read1,
  input  [15:0] IN2,
  input  [5:0] in_9,
  input  write2,
  input  read2
);

  wire clock_1_out, clock_2_out, clock_3_out;
  wire [15:0] OUT1_p1, OUT2_p1, registrador_bits16_1_saida;

  Clock clock_1 (.out(clock_1_out));
  Clock clock_2 (.out(clock_2_out));
  // LedBar #(.inputtype("row"), .matrixcols(16)) OUT2: pin names not known; wires that end beside it: OUT2_p1
  memoria_64x16 memoria_64x16_1 (
    .Adress(in_9), .write(write2), .read(read2), .IN1(IN2), .clk(clock_2_out), .OUT1(OUT2_p1));
  Clock clock_3 (.out(clock_3_out));
  // LedBar #(.inputtype("row"), .matrixcols(16)) OUT1: pin names not known; wires that end beside it: OUT1_p1
  memoria_16x16 memoria_16x16_1 (.IN1(IN1), .adress(in_5), .Ei(Write1), .Li(Read1), .clock(clock_1_out), .S(OUT1_p1));
  _7_Segment_Display u_7_segment_display_1 (.g(1'b1), .f(1'b1), .b(1'b1), .e(1'b1), .c(1'b1));  // open: a, d, dp
  registrador_bits16 registrador_bits16_1 (
    .ENTRADA(IN0), .Li(read0), .Ei(write0), .CLK(clock_3_out), .SAIDA(registrador_bits16_1_saida));  // open: CLR
  Hex_Digit_Display hex_digit_display_1 (.value(in_5));  // open: dp
  _7_Segment_Display u_7_segment_display_2 (.g(1'b1), .f(1'b1), .b(1'b1), .e(1'b1), .c(1'b1));  // open: a, d, dp
  Hex_Digit_Display hex_digit_display_2 (.value({2'b00, in_9[5:4]}));  // open: dp
  // LedBar #(.inputtype("row"), .matrixcols(16)) OUT0: pin names not known; wires that end beside it: registrador_bits16_1_saida
  Hex_Digit_Display hex_digit_display_3 (.value(in_9[3:0]));  // open: dp

  // Notes on the sheet:
  //   Memória de 64 endereços que guardam 16 bits cada
  //   Memória de 16 endereços que guardam 16 bits cada
  //   Registrador de 16 bits
  //   por trás de cada endereço existe um registrador
  //   << Memória sendo acessada
  //   << Memória sendo acessada
endmodule

module registrador_bits16 (
  input  [15:0] ENTRADA,
  input  Li,
  input  Ei,
  input  CLR,
  input  CLK,
  output [15:0] SAIDA
);

  wire buffer1_1_out_2, buffer1_2_out_2, buffer1_3_out_2, buffer1_4_out_2, buffer1_5_out_2, buffer1_6_out_2,
       buffer1_7_out_2, buffer1_8_out_2, buffer1_9_out_2, buffer1_11_out_2, buffer1_12_out_2,
       buffer1_13_out_2, buffer1_14_out_2, buffer1_15_out_2, buffer1_16_out_2, flipflopd_1_q, flipflopd_2_q,
       flipflopd_3_q, flipflopd_4_q, flipflopd_5_q, flipflopd_6_q, flipflopd_7_q, flipflopd_8_q,
       flipflopd_9_q, flipflopd_10_q, flipflopd_11_q, flipflopd_12_q, flipflopd_13_q, flipflopd_14_q,
       flipflopd_15_q, flipflopd_16_q;

  buffer1 buffer1_1 (.in_1(ENTRADA[1]), .out_2(buffer1_1_out_2));
  buffer1 buffer1_2 (.in_1(ENTRADA[2]), .out_2(buffer1_2_out_2));
  buffer1 buffer1_3 (.in_1(ENTRADA[3]), .out_2(buffer1_3_out_2));
  buffer1 buffer1_4 (.in_1(ENTRADA[4]), .out_2(buffer1_4_out_2));
  buffer1 buffer1_5 (.in_1(ENTRADA[5]), .out_2(buffer1_5_out_2));
  buffer1 buffer1_6 (.in_1(ENTRADA[6]), .out_2(buffer1_6_out_2));
  buffer1 buffer1_7 (.in_1(ENTRADA[7]), .out_2(buffer1_7_out_2));
  buffer1 buffer1_8 (.in_1(ENTRADA[8]), .out_2(buffer1_8_out_2));
  buffer1 buffer1_9 (.in_1(ENTRADA[9]), .out_2(buffer1_9_out_2));
  buffer1 buffer1_10 (.in_1(ENTRADA[10]), .out_2(Li));
  buffer1 buffer1_11 (.in_1(ENTRADA[11]), .out_2(buffer1_11_out_2));
  buffer1 buffer1_12 (.in_1(ENTRADA[12]), .out_2(buffer1_12_out_2));
  buffer1 buffer1_13 (.in_1(ENTRADA[13]), .out_2(buffer1_13_out_2));
  buffer1 buffer1_14 (.in_1(ENTRADA[14]), .out_2(buffer1_14_out_2));
  buffer1 buffer1_15 (.in_1(ENTRADA[15]), .out_2(buffer1_15_out_2));
  buffer1 buffer1_16 (.in_1(ENTRADA[0]), .out_2(buffer1_16_out_2));
  flipflopD flipflopd_1 (.Clk(CLK), .Int(buffer1_16_out_2), .Q(flipflopd_1_q));  // open: Q1
  flipflopD flipflopd_2 (.Clk(CLK), .Int(buffer1_1_out_2), .Q(flipflopd_2_q));  // open: Q1
  flipflopD flipflopd_3 (.Clk(CLK), .Int(buffer1_2_out_2), .Q(flipflopd_3_q));  // open: Q1
  flipflopD flipflopd_4 (.Clk(CLK), .Int(buffer1_3_out_2), .Q(flipflopd_4_q));  // open: Q1
  flipflopD flipflopd_5 (.Clk(CLK), .Int(buffer1_4_out_2), .Q(flipflopd_5_q));  // open: Q1
  flipflopD flipflopd_6 (.Clk(CLK), .Int(buffer1_5_out_2), .Q(flipflopd_6_q));  // open: Q1
  flipflopD flipflopd_7 (.Clk(CLK), .Int(buffer1_6_out_2), .Q(flipflopd_7_q));  // open: Q1
  flipflopD flipflopd_8 (.Clk(CLK), .Int(buffer1_7_out_2), .Q(flipflopd_8_q));  // open: Q1
  flipflopD flipflopd_9 (.Clk(CLK), .Int(buffer1_8_out_2), .Q(flipflopd_9_q));  // open: Q1
  flipflopD flipflopd_10 (.Clk(CLK), .Int(buffer1_9_out_2), .Q(flipflopd_10_q));  // open: Q1
  flipflopD flipflopd_11 (.Clk(CLK), .Int(Li), .Q(flipflopd_11_q));  // open: Q1
  flipflopD flipflopd_12 (.Clk(CLK), .Int(buffer1_11_out_2), .Q(flipflopd_12_q));  // open: Q1
  flipflopD flipflopd_13 (.Clk(CLK), .Int(buffer1_12_out_2), .Q(flipflopd_13_q));  // open: Q1
  flipflopD flipflopd_14 (.Clk(CLK), .Int(buffer1_13_out_2), .Q(flipflopd_14_q));  // open: Q1
  flipflopD flipflopd_15 (.Clk(CLK), .Int(buffer1_14_out_2), .Q(flipflopd_15_q));  // open: Q1
  flipflopD flipflopd_16 (.Clk(CLK), .Int(buffer1_15_out_2), .Q(flipflopd_16_q));  // open: Q1
  buffer1 buffer1_17 (.in_1(flipflopd_1_q), .out_2(SAIDA[0]));
  buffer1 buffer1_18 (.in_1(flipflopd_2_q), .out_2(SAIDA[1]));
  buffer1 buffer1_19 (.in_1(flipflopd_3_q), .out_2(SAIDA[2]));
  buffer1 buffer1_20 (.in_1(flipflopd_4_q), .out_2(SAIDA[3]));
  buffer1 buffer1_21 (.in_1(flipflopd_5_q), .out_2(SAIDA[4]));
  buffer1 buffer1_22 (.in_1(flipflopd_6_q), .out_2(SAIDA[5]));
  buffer1 buffer1_23 (.in_1(flipflopd_7_q), .out_2(SAIDA[6]));
  buffer1 buffer1_24 (.in_1(flipflopd_8_q), .out_2(SAIDA[7]));
  buffer1 buffer1_25 (.in_1(flipflopd_9_q), .out_2(SAIDA[8]));
  buffer1 buffer1_26 (.in_1(flipflopd_10_q), .out_2(SAIDA[9]));
  buffer1 buffer1_27 (.in_1(flipflopd_11_q), .out_2(SAIDA[10]));
  buffer1 buffer1_28 (.in_1(flipflopd_12_q), .out_2(SAIDA[11]));
  buffer1 buffer1_29 (.in_1(flipflopd_13_q), .out_2(SAIDA[12]));
  buffer1 buffer1_30 (.in_1(flipflopd_14_q), .out_2(SAIDA[13]));
  buffer1 buffer1_31 (.in_1(flipflopd_15_q), .out_2(SAIDA[14]));
  buffer1 buffer1_32 (.in_1(flipflopd_16_q), .out_2(SAIDA[15]));
endmodule

module memoria_16x16 (
  input  clock,
  input  [15:0] IN1,
  input  Li,
  input  Ei,
  input  [3:0] adress,
  output [15:0] S
);

  wire [1:0] demultiplexer_1_out0, demultiplexer_1_out1, demultiplexer_1_out2, demultiplexer_1_out3,
       demultiplexer_1_out4, demultiplexer_1_out5, demultiplexer_1_out6, demultiplexer_1_out7,
       demultiplexer_1_out8, demultiplexer_1_out9, demultiplexer_1_out10, demultiplexer_1_out11,
       demultiplexer_1_out12, demultiplexer_1_out13, demultiplexer_1_out14, demultiplexer_1_out15;
  wire [15:0] R0_saida, R1_saida, R2_saida, R3_saida, R4_saida, R5_saida, R6_saida, R7_saida, R9_saida,
       R10_saida, R11_saida, R12_saida, R13_saida, R14_saida, R15_saida;

  registrador_bits16 R0 (
    .ENTRADA(IN1), .Li(demultiplexer_1_out0[0]), .Ei(demultiplexer_1_out0[1]), .CLK(clock), .SAIDA(R0_saida));  // open: CLR
  registrador_bits16 R1 (
    .ENTRADA(IN1), .Li(demultiplexer_1_out1[0]), .Ei(demultiplexer_1_out1[1]), .CLK(clock), .SAIDA(R1_saida));  // open: CLR
  registrador_bits16 R2 (
    .ENTRADA(IN1), .Li(demultiplexer_1_out2[0]), .Ei(demultiplexer_1_out2[1]), .CLK(clock), .SAIDA(R2_saida));  // open: CLR
  registrador_bits16 R3 (
    .ENTRADA(IN1), .Li(demultiplexer_1_out3[0]), .Ei(demultiplexer_1_out3[1]), .CLK(clock), .SAIDA(R3_saida));  // open: CLR
  registrador_bits16 R4 (
    .ENTRADA(IN1), .Li(demultiplexer_1_out4[0]), .Ei(demultiplexer_1_out4[1]), .CLK(clock), .SAIDA(R4_saida));  // open: CLR
  registrador_bits16 R5 (
    .ENTRADA(IN1), .Li(demultiplexer_1_out5[0]), .Ei(demultiplexer_1_out5[1]), .CLK(clock), .SAIDA(R5_saida));  // open: CLR
  registrador_bits16 R6 (
    .ENTRADA(IN1), .Li(demultiplexer_1_out6[0]), .Ei(demultiplexer_1_out6[1]), .CLK(clock), .SAIDA(R6_saida));  // open: CLR
  registrador_bits16 R7 (
    .ENTRADA(IN1), .Li(demultiplexer_1_out7[0]), .Ei(demultiplexer_1_out7[1]), .CLK(clock), .SAIDA(R7_saida));  // open: CLR
  registrador_bits16 R8 (
    .ENTRADA(IN1), .Li(demultiplexer_1_out8[0]), .Ei(demultiplexer_1_out8[1]), .CLK(clock), .SAIDA(S));  // open: CLR
  registrador_bits16 R9 (
    .ENTRADA(IN1), .Li(demultiplexer_1_out9[0]), .Ei(demultiplexer_1_out9[1]), .CLK(clock), .SAIDA(R9_saida));  // open: CLR
  registrador_bits16 R10 (
    .ENTRADA(IN1), .Li(demultiplexer_1_out10[0]), .Ei(demultiplexer_1_out10[1]), .CLK(clock),
    .SAIDA(R10_saida));  // open: CLR
  registrador_bits16 R11 (
    .ENTRADA(IN1), .Li(demultiplexer_1_out11[0]), .Ei(demultiplexer_1_out11[1]), .CLK(clock),
    .SAIDA(R11_saida));  // open: CLR
  registrador_bits16 R12 (
    .ENTRADA(IN1), .Li(demultiplexer_1_out12[0]), .Ei(demultiplexer_1_out12[1]), .CLK(clock),
    .SAIDA(R12_saida));  // open: CLR
  registrador_bits16 R13 (
    .ENTRADA(IN1), .Li(demultiplexer_1_out13[0]), .Ei(demultiplexer_1_out13[1]), .CLK(clock),
    .SAIDA(R13_saida));  // open: CLR
  registrador_bits16 R14 (
    .ENTRADA(IN1), .Li(demultiplexer_1_out14[0]), .Ei(demultiplexer_1_out14[1]), .CLK(clock),
    .SAIDA(R14_saida));  // open: CLR
  registrador_bits16 R15 (
    .ENTRADA(IN1), .Li(demultiplexer_1_out15[0]), .Ei(demultiplexer_1_out15[1]), .CLK(clock),
    .SAIDA(R15_saida));  // open: CLR
  Demultiplexer #(.select(4), .width(2)) demultiplexer_1 (
    .out0(demultiplexer_1_out0), .out1(demultiplexer_1_out1), .out2(demultiplexer_1_out2),
    .out3(demultiplexer_1_out3), .out4(demultiplexer_1_out4), .out5(demultiplexer_1_out5),
    .out6(demultiplexer_1_out6), .out7(demultiplexer_1_out7), .out8(demultiplexer_1_out8),
    .out9(demultiplexer_1_out9), .out10(demultiplexer_1_out10), .out11(demultiplexer_1_out11),
    .out12(demultiplexer_1_out12), .out13(demultiplexer_1_out13), .out14(demultiplexer_1_out14),
    .out15(demultiplexer_1_out15), .in({Ei, Li}), .sel(adress));
  Multiplexer #(.select(4), .width(16)) multiplexer_1 (
    .in0(R0_saida), .in1(R1_saida), .in2(R2_saida), .in3(R3_saida), .in4(R4_saida), .in5(R5_saida),
    .in6(R6_saida), .in7(R7_saida), .in8(S), .in9(R9_saida), .in10(R10_saida), .in11(R11_saida),
    .in12(R12_saida), .in13(R13_saida), .in14(R14_saida), .in15(R15_saida), .out(S), .sel(adress));
endmodule

module memoria_64x16 (
  input  clk,
  input  [15:0] IN1,
  input  write,
  input  read,
  input  [5:0] Adress,
  output [15:0] OUT1
);

  wire demultiplexer_1_out0, demultiplexer_1_out1, demultiplexer_1_out2, demultiplexer_1_out3;
  wire [1:0] controlled_buffer_1_out, controlled_buffer_2_out, controlled_buffer_3_out,
       controlled_buffer_4_out;
  wire [15:0] R0_16x16_s, R1_16x16_s, R2_16x16_s, R3_16x16_s;

  Demultiplexer #(.select(2)) demultiplexer_1 (
    .out0(demultiplexer_1_out0), .out1(demultiplexer_1_out1), .out2(demultiplexer_1_out2),
    .out3(demultiplexer_1_out3), .in(1'b1), .sel(Adress[5:4]));
  assign controlled_buffer_1_out = demultiplexer_1_out0 ? {read, write} : 2'bz;  // Controlled_Buffer controlled_buffer_1
  assign controlled_buffer_2_out = demultiplexer_1_out1 ? {read, write} : 2'bz;  // Controlled_Buffer controlled_buffer_2
  assign controlled_buffer_3_out = demultiplexer_1_out2 ? {read, write} : 2'bz;  // Controlled_Buffer controlled_buffer_3
  assign controlled_buffer_4_out = demultiplexer_1_out3 ? {read, write} : 2'bz;  // Controlled_Buffer controlled_buffer_4
  memoria_16x16 R0_16x16 (
    .IN1(IN1), .adress(Adress[3:0]), .Ei(controlled_buffer_1_out[0]), .Li(controlled_buffer_1_out[1]),
    .clock(clk), .S(R0_16x16_s));
  memoria_16x16 R1_16x16 (
    .IN1(IN1), .adress(Adress[3:0]), .Ei(controlled_buffer_2_out[0]), .Li(controlled_buffer_2_out[1]),
    .clock(clk), .S(R1_16x16_s));
  memoria_16x16 R2_16x16 (
    .IN1(IN1), .adress(Adress[3:0]), .Ei(controlled_buffer_3_out[0]), .Li(controlled_buffer_3_out[1]),
    .clock(clk), .S(R2_16x16_s));
  memoria_16x16 R3_16x16 (
    .IN1(IN1), .adress(Adress[3:0]), .Ei(controlled_buffer_4_out[0]), .Li(controlled_buffer_4_out[1]),
    .clock(clk), .S(R3_16x16_s));
  Multiplexer #(.select(2), .width(16)) multiplexer_1 (
    .in0(R0_16x16_s), .in1(R1_16x16_s), .in2(R2_16x16_s), .in3(R3_16x16_s), .out(OUT1), .sel(Adress[5:4]));
endmodule

module flipflopD (
  input  Int,
  input  Clk,
  output Q,
  output Q1
);

  wire nand_1_out, nand_2_out, not_1_out;

  not not_1 (not_1_out, Int);
  nand nand_1 (nand_1_out, ~Clk, not_1_out);  // NAND_Gate
  nand nand_2 (nand_2_out, Int, Clk);
  nand nand_3 (Q, nand_2_out, Q1);
  nand nand_4 (Q1, Q, nand_1_out);
endmodule

module somador_1bit (
  input  A,
  input  B,
  input  Cin,
  output Cont,
  output Soma
);

  wire and_1_out, and_2_out, and_3_out, and_4_out, and_5_out, xor_1_out, xor_2_out;

  and and_1 (and_1_out, A, B);
  and and_2 (and_2_out, A, Cin);
  and and_3 (and_3_out, B, Cin);
  xor xor_1 (xor_1_out, A, B);
  xor xor_2 (xor_2_out, A, B);
  and and_4 (and_4_out, ~xor_1_out, Cin);  // AND_Gate
  and and_5 (and_5_out, xor_2_out, ~Cin);  // AND_Gate
  or or_1 (Cont, and_1_out, and_2_out, and_3_out);
  or or_2 (Soma, and_4_out, and_5_out);
endmodule

module somador_subtrator_1bit (
  input  in_1,
  input  in_2,
  input  in_3,
  input  in_4,
  output out_5,
  output out_6
);

  wire xor_1_out;

  xor xor_1 (xor_1_out, in_2, in_4);
  somador_1bit somador_1bit_1 (.A(in_3), .B(xor_1_out), .Cin(in_1), .Cont(out_6), .Soma(out_5));
endmodule

module somador_subtrador_8bits (
  input  Sub,
  input  [7:0] in_2,
  input  [7:0] in_3,
  output [7:0] out_4,
  output out_5,
  output Negative,
  output Cout
);

  wire somador_subtrator_1bit_1_out_6, somador_subtrator_1bit_2_out_6, somador_subtrator_1bit_3_out_6,
       somador_subtrator_1bit_4_out_6, somador_subtrator_1bit_5_out_6, somador_subtrator_1bit_6_out_6,
       somador_subtrator_1bit_7_out_6;

  somador_subtrator_1bit somador_subtrator_1bit_1 (
    .in_2(Sub), .in_1(Sub), .in_3(in_2[0]), .in_4(in_3[0]), .out_6(somador_subtrator_1bit_1_out_6),
    .out_5(out_4[0]));
  somador_subtrator_1bit somador_subtrator_1bit_2 (
    .in_2(Sub), .in_1(somador_subtrator_1bit_1_out_6), .in_3(in_2[1]), .in_4(in_3[1]),
    .out_6(somador_subtrator_1bit_2_out_6), .out_5(out_4[1]));
  somador_subtrator_1bit somador_subtrator_1bit_3 (
    .in_2(Sub), .in_1(somador_subtrator_1bit_2_out_6), .in_3(in_2[2]), .in_4(in_3[2]),
    .out_6(somador_subtrator_1bit_3_out_6), .out_5(out_4[2]));
  somador_subtrator_1bit somador_subtrator_1bit_4 (
    .in_2(Sub), .in_1(somador_subtrator_1bit_3_out_6), .in_3(in_2[3]), .in_4(in_3[3]),
    .out_6(somador_subtrator_1bit_4_out_6), .out_5(out_4[3]));
  somador_subtrator_1bit somador_subtrator_1bit_5 (
    .in_2(Sub), .in_1(somador_subtrator_1bit_4_out_6), .in_3(in_2[4]), .in_4(in_3[4]),
    .out_6(somador_subtrator_1bit_5_out_6), .out_5(out_4[4]));
  somador_subtrator_1bit somador_subtrator_1bit_6 (
    .in_2(Sub), .in_1(somador_subtrator_1bit_5_out_6), .in_3(in_2[5]), .in_4(in_3[5]),
    .out_6(somador_subtrator_1bit_6_out_6), .out_5(out_4[5]));
  somador_subtrator_1bit somador_subtrator_1bit_7 (
    .in_2(Sub), .in_1(somador_subtrator_1bit_6_out_6), .in_3(in_2[6]), .in_4(in_3[6]),
    .out_6(somador_subtrator_1bit_7_out_6), .out_5(out_4[6]));
  somador_subtrator_1bit somador_subtrator_1bit_8 (
    .in_2(Sub), .in_1(somador_subtrator_1bit_7_out_6), .in_3(in_2[7]), .in_4(in_3[7]), .out_6(Cout),
    .out_5(Negative));
  and and_1 (out_5, ~out_4[0], ~out_4[1], ~out_4[2], ~out_4[3], ~out_4[4], ~out_4[5], ~out_4[6], ~Negative);  // AND_Gate

  assign out_4[7] = Negative;

  // Notes on the sheet:
  //   A
  //   B
  //   S
endmodule

module Transfereciad_registrador (
  input  in_1,
  input  in_2,
  output out_3
);

  wire flipflopd_1_q, flipflopd_2_q, flipflopd_3_q;

  flipflopD flipflopd_1 (.Clk(in_2), .Int(in_1), .Q(flipflopd_1_q));  // open: Q1
  flipflopD flipflopd_2 (.Clk(in_2), .Int(flipflopd_1_q), .Q(flipflopd_2_q));  // open: Q1
  flipflopD flipflopd_3 (.Clk(in_2), .Int(flipflopd_2_q), .Q(flipflopd_3_q));  // open: Q1
  flipflopD flipflopd_4 (.Clk(in_2), .Int(flipflopd_3_q), .Q(out_3));  // open: Q1
endmodule

module buffer1 (
  input  in_1,
  output out_2
);

  and and_1 (out_2, in_1, in_1);
endmodule

module Demux (
  input  [3:0] E,
  output [15:0] out_2
);

  wire buffer1_1_out_2, buffer1_2_out_2, buffer1_3_out_2, buffer1_4_out_2, buffer1_5_out_2, buffer1_6_out_2,
       buffer1_7_out_2, buffer1_8_out_2, buffer1_9_out_2, buffer1_10_out_2, buffer1_11_out_2,
       buffer1_12_out_2, buffer1_13_out_2, buffer1_14_out_2, buffer1_15_out_2, buffer1_16_out_2,
       buffer1_17_out_2, buffer1_18_out_2, buffer1_19_out_2, buffer1_20_out_2, buffer1_21_out_2,
       buffer1_22_out_2, buffer1_23_out_2, buffer1_24_out_2, buffer1_25_out_2, buffer1_26_out_2,
       buffer1_27_out_2, buffer1_28_out_2, buffer1_29_out_2, buffer1_30_out_2, buffer1_31_out_2,
       buffer1_32_out_2;

  buffer1 buffer1_1 (.in_1(E[3]), .out_2(buffer1_1_out_2));
  buffer1 buffer1_2 (.in_1(E[2]), .out_2(buffer1_2_out_2));
  buffer1 buffer1_3 (.in_1(E[1]), .out_2(buffer1_3_out_2));
  buffer1 buffer1_4 (.in_1(E[0]), .out_2(buffer1_4_out_2));
  buffer1 buffer1_5 (.in_1(E[3]), .out_2(buffer1_5_out_2));
  buffer1 buffer1_6 (.in_1(E[2]), .out_2(buffer1_6_out_2));
  buffer1 buffer1_7 (.in_1(E[1]), .out_2(buffer1_7_out_2));
  buffer1 buffer1_8 (.in_1(E[3]), .out_2(buffer1_8_out_2));
  buffer1 buffer1_9 (.in_1(E[2]), .out_2(buffer1_9_out_2));
  buffer1 buffer1_10 (.in_1(E[0]), .out_2(buffer1_10_out_2));
  buffer1 buffer1_11 (.in_1(E[3]), .out_2(buffer1_11_out_2));
  buffer1 buffer1_12 (.in_1(E[2]), .out_2(buffer1_12_out_2));
  buffer1 buffer1_13 (.in_1(E[3]), .out_2(buffer1_13_out_2));
  buffer1 buffer1_14 (.in_1(E[1]), .out_2(buffer1_14_out_2));
  buffer1 buffer1_15 (.in_1(E[0]), .out_2(buffer1_15_out_2));
  buffer1 buffer1_16 (.in_1(E[3]), .out_2(buffer1_16_out_2));
  buffer1 buffer1_17 (.in_1(E[1]), .out_2(buffer1_17_out_2));
  buffer1 buffer1_18 (.in_1(E[3]), .out_2(buffer1_18_out_2));
  buffer1 buffer1_19 (.in_1(E[0]), .out_2(buffer1_19_out_2));
  buffer1 buffer1_20 (.in_1(E[3]), .out_2(buffer1_20_out_2));
  buffer1 buffer1_21 (.in_1(E[0]), .out_2(buffer1_21_out_2));
  buffer1 buffer1_22 (.in_1(E[3]), .out_2(buffer1_22_out_2));
  buffer1 buffer1_23 (.in_1(E[3]), .out_2(buffer1_23_out_2));
  buffer1 buffer1_24 (.in_1(E[2]), .out_2(buffer1_24_out_2));
  buffer1 buffer1_25 (.in_1(E[0]), .out_2(buffer1_25_out_2));
  buffer1 buffer1_26 (.in_1(E[2]), .out_2(buffer1_26_out_2));
  buffer1 buffer1_27 (.in_1(E[0]), .out_2(buffer1_27_out_2));
  buffer1 buffer1_28 (.in_1(E[2]), .out_2(buffer1_28_out_2));
  buffer1 buffer1_29 (.in_1(E[1]), .out_2(buffer1_29_out_2));
  buffer1 buffer1_30 (.in_1(E[0]), .out_2(buffer1_30_out_2));
  buffer1 buffer1_31 (.in_1(E[1]), .out_2(buffer1_31_out_2));
  buffer1 buffer1_32 (.in_1(E[0]), .out_2(buffer1_32_out_2));
  and and_1 (out_2[0], ~buffer1_1_out_2, ~buffer1_2_out_2, ~buffer1_3_out_2, ~buffer1_4_out_2);  // AND_Gate
  and and_2 (out_2[1], ~buffer1_5_out_2, ~buffer1_6_out_2, ~buffer1_7_out_2, E[0]);  // AND_Gate
  and and_3 (out_2[2], ~buffer1_8_out_2, ~buffer1_9_out_2, E[1], ~buffer1_10_out_2);  // AND_Gate
  and and_4 (out_2[3], ~buffer1_11_out_2, ~buffer1_12_out_2, E[1], E[0]);  // AND_Gate
  and and_5 (out_2[4], ~buffer1_13_out_2, E[2], ~buffer1_14_out_2, ~buffer1_15_out_2);  // AND_Gate
  and and_6 (out_2[5], ~buffer1_16_out_2, E[2], ~buffer1_17_out_2, E[0]);  // AND_Gate
  and and_7 (out_2[6], ~buffer1_18_out_2, E[2], E[1], ~buffer1_19_out_2);  // AND_Gate
  and and_8 (out_2[7], ~buffer1_20_out_2, E[2], E[1], ~buffer1_21_out_2);  // AND_Gate
  and and_9 (out_2[8], ~buffer1_22_out_2, E[2], E[1], E[0]);  // AND_Gate
  and and_10 (out_2[9], buffer1_23_out_2, ~buffer1_24_out_2, ~E[1], ~buffer1_25_out_2);  // AND_Gate
  and and_11 (out_2[10], E[3], ~buffer1_26_out_2, E[1], ~buffer1_27_out_2);  // AND_Gate
  and and_12 (out_2[11], E[3], ~buffer1_28_out_2, E[1], E[0]);  // AND_Gate
  and and_13 (out_2[12], E[3], E[2], ~buffer1_29_out_2, ~buffer1_30_out_2);  // AND_Gate
  and and_14 (out_2[13], E[3], E[2], ~buffer1_31_out_2, E[0]);  // AND_Gate
  and and_15 (out_2[14], E[3], E[2], E[1], ~buffer1_32_out_2);  // AND_Gate
  and and_16 (out_2[15], E[3], E[2], E[1], E[0]);

  // Notes on the sheet:
  //   S
endmodule

module Mux (
  input  [3:0] E,
  input  V1,
  input  V2,
  output S
);

  wire and_1_out, and_2_out, and_3_out, and_4_out;

  and and_1 (and_1_out, E[0], ~V1, ~V2);  // AND_Gate
  and and_2 (and_2_out, E[1], ~V1, V2);  // AND_Gate
  and and_3 (and_3_out, E[2], V1, ~V2);  // AND_Gate
  and and_4 (and_4_out, E[3], V1, V2);
  or or_1 (S, and_1_out, and_2_out, and_3_out, and_4_out);
endmodule

module Mux_16bit (
  input  [3:0] in_1,
  input  [15:0] in_2,
  output out_3
);

  wire [3:0] mux_1_s;

  Mux mux_1 (.E(in_2[3:0]), .V1(in_1[0]), .S(mux_1_s[0]));  // open: V2
  Mux mux_2 (.E(in_2[11:8]), .V1(in_1[0]), .V2(in_1[1]), .S(mux_1_s[2]));
  Mux mux_3 (.E(in_2[7:4]), .V1(in_1[0]), .S(mux_1_s[1]));  // open: V2
  Mux mux_4 (.E(in_2[15:12]), .V1(in_1[0]), .V2(in_1[1]), .S(mux_1_s[3]));
  Mux mux_5 (.E(mux_1_s), .V1(in_1[2]), .V2(in_1[3]), .S(out_3));
endmodule
