// Logisim project ULA_1.circ as structural Verilog: 7 circuits, main circuit main
module main (
);

  wire ALUSrc, Clear, CLK;
  wire [4:0] pc_1_out_4, undriven;
  wire [15:0] bit_extender_1_out, multiplexer_1_out, registers_8x16_1_out_8, registers_8x16_1_out_9;

  PC pc_1 (.Clock(CLK), .Clear(Clear), .in_1(undriven), .out_4(pc_1_out_4));
  assign bit_extender_1_out = {{11{pc_1_out_4[4]}}, pc_1_out_4};  // Bit_Extender bit_extender_1
  ULA16_bit ula16_bit_1 (.in_2({16{1'b1}}), .in_3(bit_extender_1_out));  // open: SEL, Negative, Zero, out_4
  ROM #(.addrWidth(5), .dataWidth(16)) rom_1 (.addr(pc_1_out_4));  // open: data
  Registers_8x16 registers_8x16_1 (
    .out_9(registers_8x16_1_out_9), .out_8(registers_8x16_1_out_8));  // open: Read2, Read1, in_1, RegWrite, Write, Reset, CLK
  ULA16_bit ula16_bit_2 (.SEL(3'b000));  // open: in_2, in_3, Negative, Zero, out_4
  Multiplexer #(.width(16)) multiplexer_1 (
    .in0(registers_8x16_1_out_9), .out(multiplexer_1_out), .sel(ALUSrc));  // open: in1
  Multiplexer #(.width(16)) multiplexer_2 ();  // open: in0, in1, out, sel
  ULA16_bit ula16_bit_3 (.in_2(registers_8x16_1_out_8), .in_3(multiplexer_1_out));  // open: SEL, Negative, Zero, out_4
  RAM #(.addrWidth(5), .dataWidth(16)) ram_1 ();  // open: addr, we, oe, clk, din, dout
endmodule

module ULA (
  input  A,
  input  B,
  input  Cin,
  input  [2:0] Sel,
  output S,
  output out_6
);

  wire and_1_out, nand_1_out, nor_1_out, or_1_out, somandor_subtrator_1bit_1_s, xor_1_out;

  somandor_subtrator_1bit somandor_subtrator_1bit_1 (
    .A(A), .B(B), .Sub(Sel[0]), .Cin(Cin), .Cout(out_6), .S(somandor_subtrator_1bit_1_s));
  and and_1 (and_1_out, B, A);
  or or_1 (or_1_out, A, B);
  xor xor_1 (xor_1_out, A, B);
  nand nand_1 (nand_1_out, A, B);
  nor nor_1 (nor_1_out, A, B);
  Multiplexer #(.select(3)) multiplexer_1 (
    .in0(somandor_subtrator_1bit_1_s), .in1(and_1_out), .in2(or_1_out), .in3(xor_1_out), .in4(nand_1_out),
    .in5(nor_1_out), .out(S), .sel(Sel));  // open: in6, in7
endmodule

module somandor_bit (
  input  A,
  input  B,
  input  Cin,
  output Cout,
  output Soma
);

  wire and_1_out, and_2_out, and_3_out, and_4_out, and_5_out, xnor_1_out, xor_1_out;

  and and_1 (and_1_out, A, B);
  and and_2 (and_2_out, A, Cin);
  and and_3 (and_3_out, B, Cin);
  xnor xnor_1 (xnor_1_out, A, B);
  xor xor_1 (xor_1_out, A, B);
  and and_4 (and_4_out, xnor_1_out, Cin);
  and and_5 (and_5_out, xor_1_out, ~Cin);  // AND_Gate
  or or_1 (Cout, and_1_out, and_2_out, and_3_out);
  or or_2 (Soma, and_4_out, and_5_out);
endmodule

module somandor_subtrator_1bit (
  input  Sub,
  input  Cin,
  input  A,
  input  B,
  output S,
  output Cout
);

  wire xor_1_out;

  xor xor_1 (xor_1_out, Sub, B);
  somandor_bit somandor_bit_1 (.A(A), .B(xor_1_out), .Cin(Cin), .Cout(S), .Soma(Cout));
endmodule

module ULA16_bit (
  input  [2:0] SEL,
  input  [15:0] in_2,
  input  [15:0] in_3,
  output [15:0] out_4,
  output Negative,
  output Zero
);

  wire and_1_out, ula_1_s, ula_2_s, ula_3_s, ula_4_s, ula_5_s, ula_6_s, ula_7_s, ula_8_s, ula_9_s, ula_10_s,
       ula_11_s, ula_12_s, ula_13_s, ula_14_s, ula_15_s;
  wire [6:0] ula_9_out_6;
  wire [7:0] ula_1_out_6;

  ULA ula_1 (.Sel(SEL), .A(in_2[0]), .B(in_3[0]), .Cin(SEL[0]), .S(ula_1_s), .out_6(ula_1_out_6[0]));
  ULA ula_2 (.Sel(SEL), .A(in_2[1]), .B(in_3[1]), .Cin(ula_1_s), .S(ula_2_s), .out_6(ula_1_out_6[1]));
  ULA ula_3 (.Sel(SEL), .A(in_2[2]), .B(in_3[2]), .Cin(ula_2_s), .S(ula_3_s), .out_6(ula_1_out_6[2]));
  ULA ula_4 (.Sel(SEL), .A(in_2[3]), .B(in_3[3]), .Cin(ula_3_s), .S(ula_4_s), .out_6(ula_1_out_6[3]));
  ULA ula_5 (.Sel(SEL), .A(in_2[4]), .B(in_3[4]), .Cin(ula_4_s), .S(ula_5_s), .out_6(ula_1_out_6[4]));
  ULA ula_6 (.Sel(SEL), .A(in_2[5]), .B(in_3[5]), .Cin(ula_5_s), .S(ula_6_s), .out_6(ula_1_out_6[5]));
  ULA ula_7 (.Sel(SEL), .A(in_2[6]), .B(in_3[6]), .Cin(ula_6_s), .S(ula_7_s), .out_6(ula_1_out_6[6]));
  ULA ula_8 (.Sel(SEL), .A(in_2[7]), .B(in_3[7]), .Cin(ula_7_s), .S(ula_8_s), .out_6(ula_1_out_6[7]));
  and and_1 (and_1_out, SEL[0], SEL[1], ~SEL[2]);  // AND_Gate
  ULA ula_9 (.Sel(SEL), .A(in_2[8]), .B(in_3[8]), .Cin(ula_8_s), .S(ula_9_s), .out_6(ula_9_out_6[0]));
  ULA ula_10 (.Sel(SEL), .A(in_2[9]), .B(in_3[9]), .Cin(ula_9_s), .S(ula_10_s), .out_6(ula_9_out_6[1]));
  ULA ula_11 (.Sel(SEL), .A(in_2[10]), .B(in_3[10]), .Cin(ula_10_s), .S(ula_11_s), .out_6(ula_9_out_6[2]));
  ULA ula_12 (.Sel(SEL), .A(in_2[11]), .B(in_3[11]), .Cin(ula_11_s), .S(ula_12_s), .out_6(ula_9_out_6[3]));
  ULA ula_13 (.Sel(SEL), .A(in_2[12]), .B(in_3[12]), .Cin(ula_12_s), .S(ula_13_s), .out_6(ula_9_out_6[4]));
  ULA ula_14 (.Sel(SEL), .A(in_2[13]), .B(in_3[13]), .Cin(ula_13_s), .S(ula_14_s), .out_6(ula_9_out_6[5]));
  ULA ula_15 (.Sel(SEL), .A(in_2[14]), .B(in_3[14]), .Cin(ula_14_s), .S(ula_15_s), .out_6(ula_9_out_6[6]));
  ULA ula_16 (.Sel(SEL), .A(in_2[15]), .B(in_3[15]), .Cin(ula_15_s), .out_6(Negative));  // open: S
  Multiplexer #(.width(16)) multiplexer_1 (
    .in0({Negative, ula_9_out_6, ula_1_out_6}), .in1({{15{1'b0}}, Negative}), .out(out_4), .sel(and_1_out));
  nor nor_1 (Zero, ula_1_out_6[7], ula_1_out_6[0], ula_1_out_6[1], ula_1_out_6[2], ula_1_out_6[3], ula_1_out_6[4], ula_1_out_6[5], ula_1_out_6[6], ula_9_out_6[0], ula_9_out_6[1], ula_9_out_6[2], ula_9_out_6[3], ula_9_out_6[4], ula_9_out_6[5], ula_9_out_6[6], Negative);

  // Notes on the sheet:
  //   A
  //   B
  //   S
endmodule

module PC (
  input  [4:0] in_1,
  input  Clock,
  input  Clear,
  output [4:0] out_4
);

  D_Flip_Flop d_ff_1 (.D(in_1[4]), .clk(Clock), .Q(out_4[4]), .reset(Clear));  // open: Qn, preset
  D_Flip_Flop d_ff_2 (.D(in_1[3]), .clk(Clock), .Q(out_4[3]), .reset(Clear));  // open: Qn, preset
  D_Flip_Flop d_ff_3 (.D(in_1[2]), .clk(Clock), .Q(out_4[2]), .reset(Clear));  // open: Qn, preset
  D_Flip_Flop d_ff_4 (.D(in_1[1]), .clk(Clock), .Q(out_4[1]), .reset(Clear));  // open: Qn, preset
  D_Flip_Flop d_ff_5 (.D(in_1[0]), .clk(Clock), .Q(out_4[0]), .reset(Clear));  // open: Qn, preset

  // Notes on the sheet:
  //   Entrada
  //   Saida
endmodule

module Registers_8x16 (
  input  [15:0] in_1,
  input  RegWrite,
  input  [2:0] Read1,
  input  [2:0] Write,
  input  [2:0] Read2,
  input  Reset,
  input  CLK,
  output [15:0] out_8,
  output [15:0] out_9
);

  wire [15:0] register_1_q, register_2_q, register_3_q, register_4_q, register_5_q, register_6_q,
       register_7_q, register_8_q;
  wire [16:0] demultiplexer_1_out0, demultiplexer_1_out1, demultiplexer_1_out2, demultiplexer_1_out3,
       demultiplexer_1_out4, demultiplexer_1_out5, demultiplexer_1_out6, demultiplexer_1_out7;

  Demultiplexer #(.select(3), .width(17)) demultiplexer_1 (
    .out0(demultiplexer_1_out0), .out1(demultiplexer_1_out1), .out2(demultiplexer_1_out2),
    .out3(demultiplexer_1_out3), .out4(demultiplexer_1_out4), .out5(demultiplexer_1_out5),
    .out6(demultiplexer_1_out6), .out7(demultiplexer_1_out7), .in({RegWrite, in_1}), .sel(Write));
  Register #(.width(16)) register_1 (
    .D(demultiplexer_1_out0[15:0]), .en(demultiplexer_1_out0[16]), .clk(CLK), .Q(register_1_q), .clr(Reset));
  Register #(.width(16)) register_2 (
    .D(demultiplexer_1_out1[15:0]), .en(demultiplexer_1_out1[16]), .clk(CLK), .Q(register_2_q), .clr(Reset));
  Register #(.width(16)) register_3 (
    .D(demultiplexer_1_out2[15:0]), .en(demultiplexer_1_out2[16]), .clk(CLK), .Q(register_3_q), .clr(Reset));
  Register #(.width(16)) register_4 (
    .D(demultiplexer_1_out3[15:0]), .en(demultiplexer_1_out3[16]), .clk(CLK), .Q(register_4_q), .clr(Reset));
  Register #(.width(16)) register_5 (
    .D(demultiplexer_1_out4[15:0]), .en(demultiplexer_1_out4[16]), .clk(CLK), .Q(register_5_q), .clr(Reset));
  Register #(.width(16)) register_6 (
    .D(demultiplexer_1_out5[15:0]), .en(demultiplexer_1_out5[16]), .clk(CLK), .Q(register_6_q), .clr(Reset));
  Register #(.width(16)) register_7 (
    .D(demultiplexer_1_out6[15:0]), .en(demultiplexer_1_out6[16]), .clk(CLK), .Q(register_7_q), .clr(Reset));
  Register #(.width(16)) register_8 (
    .D(demultiplexer_1_out7[15:0]), .en(demultiplexer_1_out7[16]), .clk(CLK), .Q(register_8_q), .clr(Reset));
  Multiplexer #(.select(3), .width(16)) multiplexer_1 (
    .in0(register_1_q), .in1(register_2_q), .in2(register_3_q), .in3(register_4_q), .in4(register_5_q),
    .in5(register_6_q), .in6(register_7_q), .in7(register_8_q), .out(out_9), .sel(Read2));
  Multiplexer #(.select(3), .width(16)) multiplexer_2 (
    .in0(register_1_q), .in1(register_2_q), .in2(register_3_q), .in3(register_4_q), .in4(register_5_q),
    .in5(register_6_q), .in6(register_7_q), .in7(register_8_q), .out(out_8), .sel(Read1));

  // Notes on the sheet:
  //   Entrada
  //   R2
  //   R1
endmodule
