// Logisim project registradores_e_memoria (1).circ as structural Verilog: 5 circuits, main circuit main
module main (
  input  [15:0] IN0,
  input  write0,
  input  read0,
  input  [15:0] IN1,
  input  [3:0] in_5,
  input  Write1,
  input  Read1,
  input  [15:0] IN2,
  input  [5:0] in_9,
  input  write2,
  input  read2
);

  wire clock_1_out, clock_2_out, clock_3_out;
  wire [15:0] OUT1_p1, OUT2_p1, registrador_bits16_1_saida;

  Clock clock_1 (.out(clock_1_out));
  Clock clock_2 (.out(clock_2_out));
  // LedBar #(.inputtype("row"), .matrixcols(16)) OUT2: pin names not known; wires that end beside it: OUT2_p1
  memoria_64x16 memoria_64x16_1 (
    .Adress(in_9), .write(write2), .read(read2), .IN1(IN2), .clk(clock_2_out), .OUT1(OUT2_p1));
  Clock clock_3 (.out(clock_3_out));
  // LedBar #(.inputtype("row"), .matrixcols(16)) OUT1: pin names not known; wires that end beside it: OUT1_p1
  memoria_16x16 memoria_16x16_1 (.IN1(IN1), .adress(in_5), .Ei(Write1), .Li(Read1), .clock(clock_1_out), .S(OUT1_p1));
  _7_Segment_Display u_7_segment_display_1 (.g(1'b1), .f(1'b1), .b(1'b1), .e(1'b1), .c(1'b1));  // open: a, d, dp
  registrador_bits16 registrador_bits16_1 (
    .ENTRADA(IN0), .Li(read0), .Ei(write0), .CLK(clock_3_out), .SAIDA(registrador_bits16_1_saida));  // open: CLR
  Hex_Digit_Display hex_digit_display_1 (.value(in_5));  // open: dp
  _7_Segment_Display u_7_segment_display_2 (.g(1'b1), .f(1'b1), .b(1'b1), .e(1'b1), .c(1'b1));  // open: a, d, dp
  Hex_Digit_Display hex_digit_display_2 (.value({2'b00, in_9[5:4]}));  // open: dp
  // LedBar #(.inputtype("row"), .matrixcols(16)) OUT0: pin names not known; wires that end beside it: registrador_bits16_1_saida
  Hex_Digit_Display hex_digit_display_3 (.value(in_9[3:0]));  // open: dp

  // Notes on the sheet:
  //   Memória de 64 endereços que guardam 16 bits cada
  //   Memória de 16 endereços que guardam 16 bits cada
  //   Registrador de 16 bits
  //   por trás de cada endereço existe um registrador
  //   << Memória sendo acessada
  //   << Memória sendo acessada
endmodule

module registrador_bits16 (
  input  [15:0] ENTRADA,
  input  Li,
  input  Ei,
  input  CLR,
  input  CLK,
  output [15:0] SAIDA
);

  wire controlled_buffer_1_out, controlled_buffer_2_out, controlled_buffer_3_out, controlled_buffer_4_out,
       controlled_buffer_5_out, controlled_buffer_6_out, controlled_buffer_7_out, controlled_buffer_8_out,
       controlled_buffer_9_out, controlled_buffer_10_out, controlled_buffer_11_out, controlled_buffer_12_out,
       controlled_buffer_13_out, controlled_buffer_14_out, controlled_buffer_15_out,
       controlled_buffer_16_out, flipflopd_1_q, flipflopd_2_q, flipflopd_3_q, flipflopd_4_q, flipflopd_5_q,
       flipflopd_6_q, flipflopd_7_q, flipflopd_8_q, flipflopd_9_q, flipflopd_10_q, flipflopd_11_q,
       flipflopd_12_q, flipflopd_13_q, flipflopd_14_q, flipflopd_15_q, flipflopd_16_q;

  assign controlled_buffer_1_out = Li ? ENTRADA[0] : 1'bz;  // Controlled_Buffer controlled_buffer_1
  assign controlled_buffer_2_out = Li ? ENTRADA[1] : 1'bz;  // Controlled_Buffer controlled_buffer_2
  assign controlled_buffer_3_out = Li ? ENTRADA[2] : 1'bz;  // Controlled_Buffer controlled_buffer_3
  assign controlled_buffer_4_out = Li ? ENTRADA[3] : 1'bz;  // Controlled_Buffer controlled_buffer_4
  assign controlled_buffer_5_out = Li ? ENTRADA[4] : 1'bz;  // Controlled_Buffer controlled_buffer_5
  assign controlled_buffer_6_out = Li ? ENTRADA[5] : 1'bz;  // Controlled_Buffer controlled_buffer_6
  assign controlled_buffer_7_out = Li ? ENTRADA[6] : 1'bz;  // Controlled_Buffer controlled_buffer_7
  assign controlled_buffer_8_out = Li ? ENTRADA[7] : 1'bz;  // Controlled_Buffer controlled_buffer_8
  assign controlled_buffer_9_out = Li ? ENTRADA[8] : 1'bz;  // Controlled_Buffer controlled_buffer_9
  assign controlled_buffer_10_out = Li ? ENTRADA[9] : 1'bz;  // Controlled_Buffer controlled_buffer_10
  assign controlled_buffer_11_out = Li ? ENTRADA[10] : 1'bz;  // Controlled_Buffer controlled_buffer_11
  assign controlled_buffer_12_out = Li ? ENTRADA[11] : 1'bz;  // Controlled_Buffer controlled_buffer_12
  assign controlled_buffer_13_out = Li ? ENTRADA[12] : 1'bz;  // Controlled_Buffer controlled_buffer_13
  assign controlled_buffer_14_out = Li ? ENTRADA[13] : 1'bz;  // Controlled_Buffer controlled_buffer_14
  assign controlled_buffer_15_out = Li ? ENTRADA[14] : 1'bz;  // Controlled_Buffer controlled_buffer_15
  assign controlled_buffer_16_out = Li ? ENTRADA[15] : 1'bz;  // Controlled_Buffer controlled_buffer_16
  flipflopD flipflopd_1 (.Clk(CLK), .Int(controlled_buffer_1_out), .Q(flipflopd_1_q));  // open: Q1
  flipflopD flipflopd_2 (.Clk(CLK), .Int(controlled_buffer_2_out), .Q(flipflopd_2_q));  // open: Q1
  flipflopD flipflopd_3 (.Clk(CLK), .Int(controlled_buffer_3_out), .Q(flipflopd_3_q));  // open: Q1
  flipflopD flipflopd_4 (.Clk(CLK), .Int(controlled_buffer_4_out), .Q(flipflopd_4_q));  // open: Q1
  flipflopD flipflopd_5 (.Clk(CLK), .Int(controlled_buffer_5_out), .Q(flipflopd_5_q));  // open: Q1
  flipflopD flipflopd_6 (.Clk(CLK), .Int(controlled_buffer_6_out), .Q(flipflopd_6_q));  // open: Q1
  flipflopD flipflopd_7 (.Clk(CLK), .Int(controlled_buffer_7_out), .Q(flipflopd_7_q));  // open: Q1
  flipflopD flipflopd_8 (.Clk(CLK), .Int(controlled_buffer_8_out), .Q(flipflopd_8_q));  // open: Q1
  flipflopD flipflopd_9 (.Clk(CLK), .Int(controlled_buffer_9_out), .Q(flipflopd_9_q));  // open: Q1
  flipflopD flipflopd_10 (.Clk(CLK), .Int(controlled_buffer_10_out), .Q(flipflopd_10_q));  // open: Q1
  flipflopD flipflopd_11 (.Clk(CLK), .Int(controlled_buffer_11_out), .Q(flipflopd_11_q));  // open: Q1
  flipflopD flipflopd_12 (.Clk(CLK), .Int(controlled_buffer_12_out), .Q(flipflopd_12_q));  // open: Q1
  flipflopD flipflopd_13 (.Clk(CLK), .Int(controlled_buffer_13_out), .Q(flipflopd_13_q));  // open: Q1
  flipflopD flipflopd_14 (.Clk(CLK), .Int(controlled_buffer_14_out), .Q(flipflopd_14_q));  // open: Q1
  flipflopD flipflopd_15 (.Clk(CLK), .Int(controlled_buffer_15_out), .Q(flipflopd_15_q));  // open: Q1
  flipflopD flipflopd_16 (.Clk(CLK), .Int(controlled_buffer_16_out), .Q(flipflopd_16_q));  // open: Q1
  assign SAIDA[0] = Ei ? flipflopd_1_q : 1'bz;  // Controlled_Buffer controlled_buffer_17
  assign SAIDA[1] = Ei ? flipflopd_2_q : 1'bz;  // Controlled_Buffer controlled_buffer_18
  assign SAIDA[2] = Ei ? flipflopd_3_q : 1'bz;  // Controlled_Buffer controlled_buffer_19
  assign SAIDA[3] = Ei ? flipflopd_4_q : 1'bz;  // Controlled_Buffer controlled_buffer_20
  assign SAIDA[4] = Ei ? flipflopd_5_q : 1'bz;  // Controlled_Buffer controlled_buffer_21
  assign SAIDA[5] = Ei ? flipflopd_6_q : 1'bz;  // Controlled_Buffer controlled_buffer_22
  assign SAIDA[6] = Ei ? flipflopd_7_q : 1'bz;  // Controlled_Buffer controlled_buffer_23
  assign SAIDA[7] = Ei ? flipflopd_8_q : 1'bz;  // Controlled_Buffer controlled_buffer_24
  assign SAIDA[8] = Ei ? flipflopd_9_q : 1'bz;  // Controlled_Buffer controlled_buffer_25
  assign SAIDA[9] = Ei ? flipflopd_10_q : 1'bz;  // Controlled_Buffer controlled_buffer_26
  assign SAIDA[10] = Ei ? flipflopd_11_q : 1'bz;  // Controlled_Buffer controlled_buffer_27
  assign SAIDA[11] = Ei ? flipflopd_12_q : 1'bz;  // Controlled_Buffer controlled_buffer_28
  assign SAIDA[12] = Ei ? flipflopd_13_q : 1'bz;  // Controlled_Buffer controlled_buffer_29
  assign SAIDA[13] = Ei ? flipflopd_14_q : 1'bz;  // Controlled_Buffer controlled_buffer_30
  assign SAIDA[14] = Ei ? flipflopd_15_q : 1'bz;  // Controlled_Buffer controlled_buffer_31
  assign SAIDA[15] = Ei ? flipflopd_16_q : 1'bz;  // Controlled_Buffer controlled_buffer_32
endmodule

module memoria_16x16 (
  input  clock,
  input  [15:0] IN1,
  input  Li,
  input  Ei,
  input  [3:0] adress,
  output [15:0] S
);

  wire [1:0] demultiplexer_1_out0, demultiplexer_1_out1, demultiplexer_1_out2, demultiplexer_1_out3,
       demultiplexer_1_out4, demultiplexer_1_out5, demultiplexer_1_out6, demultiplexer_1_out7,
       demultiplexer_1_out8, demultiplexer_1_out9, demultiplexer_1_out10, demultiplexer_1_out11,
       demultiplexer_1_out12, demultiplexer_1_out13, demultiplexer_1_out14, demultiplexer_1_out15;
  wire [15:0] R0_saida, R1_saida, R2_saida, R3_saida, R4_saida, R5_saida, R6_saida, R7_saida, R9_saida,
       R10_saida, R11_saida, R12_saida, R13_saida, R14_saida, R15_saida;

  registrador_bits16 R0 (
    .ENTRADA(IN1), .Li(demultiplexer_1_out0[0]), .Ei(demultiplexer_1_out0[1]), .CLK(clock), .SAIDA(R0_saida));  // open: CLR
  registrador_bits16 R1 (
    .ENTRADA(IN1), .Li(demultiplexer_1_out1[0]), .Ei(demultiplexer_1_out1[1]), .CLK(clock), .SAIDA(R1_saida));  // open: CLR
  registrador_bits16 R2 (
    .ENTRADA(IN1), .Li(demultiplexer_1_out2[0]), .Ei(demultiplexer_1_out2[1]), .CLK(clock), .SAIDA(R2_saida));  // open: CLR
  registrador_bits16 R3 (
    .ENTRADA(IN1), .Li(demultiplexer_1_out3[0]), .Ei(demultiplexer_1_out3[1]), .CLK(clock), .SAIDA(R3_saida));  // open: CLR
  registrador_bits16 R4 (
    .ENTRADA(IN1), .Li(demultiplexer_1_out4[0]), .Ei(demultiplexer_1_out4[1]), .CLK(clock), .SAIDA(R4_saida));  // open: CLR
  registrador_bits16 R5 (
    .ENTRADA(IN1), .Li(demultiplexer_1_out5[0]), .Ei(demultiplexer_1_out5[1]), .CLK(clock), .SAIDA(R5_saida));  // open: CLR
  registrador_bits16 R6 (
    .ENTRADA(IN1), .Li(demultiplexer_1_out6[0]), .Ei(demultiplexer_1_out6[1]), .CLK(clock), .SAIDA(R6_saida));  // open: CLR
  registrador_bits16 R7 (
    .ENTRADA(IN1), .Li(demultiplexer_1_out7[0]), .Ei(demultiplexer_1_out7[1]), .CLK(clock), .SAIDA(R7_saida));  // open: CLR
  registrador_bits16 R8 (
    .ENTRADA(IN1), .Li(demultiplexer_1_out8[0]), .Ei(demultiplexer_1_out8[1]), .CLK(clock), .SAIDA(S));  // open: CLR
  registrador_bits16 R9 (
    .ENTRADA(IN1), .Li(demultiplexer_1_out9[0]), .Ei(demultiplexer_1_out9[1]), .CLK(clock), .SAIDA(R9_saida));  // open: CLR
  registrador_bits16 R10 (
    .ENTRADA(IN1), .Li(demultiplexer_1_out10[0]), .Ei(demultiplexer_1_out10[1]), .CLK(clock),
    .SAIDA(R10_saida));  // open: CLR
  registrador_bits16 R11 (
    .ENTRADA(IN1), .Li(demultiplexer_1_out11[0]), .Ei(demultiplexer_1_out11[1]), .CLK(clock),
    .SAIDA(R11_saida));  // open: CLR
  registrador_bits16 R12 (
    .ENTRADA(IN1), .Li(demultiplexer_1_out12[0]), .Ei(demultiplexer_1_out12[1]), .CLK(clock),
    .SAIDA(R12_saida));  // open: CLR
  registrador_bits16 R13 (
    .ENTRADA(IN1), .Li(demultiplexer_1_out13[0]), .Ei(demultiplexer_1_out13[1]), .CLK(clock),
    .SAIDA(R13_saida));  // open: CLR
  registrador_bits16 R14 (
    .ENTRADA(IN1), .Li(demultiplexer_1_out14[0]), .Ei(demultiplexer_1_out14[1]), .CLK(clock),
    .SAIDA(R14_saida));  // open: CLR
  registrador_bits16 R15 (
    .ENTRADA(IN1), .Li(demultiplexer_1_out15[0]), .Ei(demultiplexer_1_out15[1]), .CLK(clock),
    .SAIDA(R15_saida));  // open: CLR
  Demultiplexer #(.select(4), .width(2)) demultiplexer_1 (
    .out0(demultiplexer_1_out0), .out1(demultiplexer_1_out1), .out2(demultiplexer_1_out2),
    .out3(demultiplexer_1_out3), .out4(demultiplexer_1_out4), .out5(demultiplexer_1_out5),
    .out6(demultiplexer_1_out6), .out7(demultiplexer_1_out7), .out8(demultiplexer_1_out8),
    .out9(demultiplexer_1_out9), .out10(demultiplexer_1_out10), .out11(demultiplexer_1_out11),
    .out12(demultiplexer_1_out12), .out13(demultiplexer_1_out13), .out14(demultiplexer_1_out14),
    .out15(demultiplexer_1_out15), .in({Ei, Li}), .sel(adress));
  Multiplexer #(.select(4), .width(16)) multiplexer_1 (
    .in0(R0_saida), .in1(R1_saida), .in2(R2_saida), .in3(R3_saida), .in4(R4_saida), .in5(R5_saida),
    .in6(R6_saida), .in7(R7_saida), .in8(S), .in9(R9_saida), .in10(R10_saida), .in11(R11_saida),
    .in12(R12_saida), .in13(R13_saida), .in14(R14_saida), .in15(R15_saida), .out(S), .sel(adress));
endmodule

module memoria_64x16 (
  input  clk,
  input  [15:0] IN1,
  input  write,
  input  read,
  input  [5:0] Adress,
  output [15:0] OUT1
);

  wire demultiplexer_1_out0, demultiplexer_1_out1, demultiplexer_1_out2, demultiplexer_1_out3;
  wire [1:0] controlled_buffer_1_out, controlled_buffer_2_out, controlled_buffer_3_out,
       controlled_buffer_4_out;
  wire [15:0] R0_16x16_s, R1_16x16_s, R2_16x16_s, R3_16x16_s;

  Demultiplexer #(.select(2)) demultiplexer_1 (
    .out0(demultiplexer_1_out0), .out1(demultiplexer_1_out1), .out2(demultiplexer_1_out2),
    .out3(demultiplexer_1_out3), .in(1'b1), .sel(Adress[5:4]));
  assign controlled_buffer_1_out = demultiplexer_1_out0 ? {read, write} : 2'bz;  // Controlled_Buffer controlled_buffer_1
  assign controlled_buffer_2_out = demultiplexer_1_out1 ? {read, write} : 2'bz;  // Controlled_Buffer controlled_buffer_2
  assign controlled_buffer_3_out = demultiplexer_1_out2 ? {read, write} : 2'bz;  // Controlled_Buffer controlled_buffer_3
  assign controlled_buffer_4_out = demultiplexer_1_out3 ? {read, write} : 2'bz;  // Controlled_Buffer controlled_buffer_4
  memoria_16x16 R0_16x16 (
    .IN1(IN1), .adress(Adress[3:0]), .Ei(controlled_buffer_1_out[0]), .Li(controlled_buffer_1_out[1]),
    .clock(clk), .S(R0_16x16_s));
  memoria_16x16 R1_16x16 (
    .IN1(IN1), .adress(Adress[3:0]), .Ei(controlled_buffer_2_out[0]), .Li(controlled_buffer_2_out[1]),
    .clock(clk), .S(R1_16x16_s));
  memoria_16x16 R2_16x16 (
    .IN1(IN1), .adress(Adress[3:0]), .Ei(controlled_buffer_3_out[0]), .Li(controlled_buffer_3_out[1]),
    .clock(clk), .S(R2_16x16_s));
  memoria_16x16 R3_16x16 (
    .IN1(IN1), .adress(Adress[3:0]), .Ei(controlled_buffer_4_out[0]), .Li(controlled_buffer_4_out[1]),
    .clock(clk), .S(R3_16x16_s));
  Multiplexer #(.select(2), .width(16)) multiplexer_1 (
    .in0(R0_16x16_s), .in1(R1_16x16_s), .in2(R2_16x16_s), .in3(R3_16x16_s), .out(OUT1), .sel(Adress[5:4]));
endmodule

module flipflopD (
  input  Int,
  input  Clk,
  output Q,
  output Q1
);

  wire nand_1_out, nand_2_out, not_1_out;

  not not_1 (not_1_out, Int);
  nand nand_1 (nand_1_out, ~Clk, not_1_out);  // NAND_Gate
  nand nand_2 (nand_2_out, Int, Clk);
  nand nand_3 (Q, nand_2_out, Q1);
  nand nand_4 (Q1, Q, nand_1_out);
endmodule
