// Logisim project registradores_e_memoria.circ as structural Verilog: 4 circuits, main circuit main
module main (
  input  [7:0] IN0,
  input  write0,
  input  read0,
  input  [7:0] IN1,
  input  [3:0] in_5,
  input  Write1,
  input  Read1,
  input  [7:0] IN2,
  input  [5:0] in_9,
  input  write2,
  input  read2
);

  wire clock_1_out, clock_2_out, clock_3_out;
  wire [7:0] OUT1_p1, OUT2_p1, registrador_8bits_1_s;

  Clock clock_1 (.out(clock_1_out));
  Clock clock_2 (.out(clock_2_out));
  // LedBar #(.inputtype("row")) OUT2: pin names not known; wires that end beside it: OUT2_p1
  memoria_64x8 memoria_64x8_1 (
    .Adress(in_9), .write(write2), .read(read2), .IN1(IN2), .clk(clock_2_out), .OUT1(OUT2_p1));
  Clock clock_3 (.out(clock_3_out));
  // LedBar #(.inputtype("row")) OUT1: pin names not known; wires that end beside it: OUT1_p1
  memoria_16x8 memoria_16x8_1 (
    .read(Read1), .write(Write1), .adress(in_5), .IN1(IN1), .clock(clock_1_out), .S(OUT1_p1));
  _7_Segment_Display u_7_segment_display_1 (.g(1'b1), .f(1'b1), .b(1'b1), .e(1'b1), .c(1'b1));  // open: a, d, dp
  registrador_8bits registrador_8bits_1 (
    .clock(clock_3_out), .write(write0), .A(IN0), .read(read0), .S(registrador_8bits_1_s));
  Hex_Digit_Display hex_digit_display_1 (.value(in_5));  // open: dp
  _7_Segment_Display u_7_segment_display_2 (.g(1'b1), .f(1'b1), .b(1'b1), .e(1'b1), .c(1'b1));  // open: a, d, dp
  Hex_Digit_Display hex_digit_display_2 (.value({2'b00, in_9[5:4]}));  // open: dp
  // LedBar #(.inputtype("row")) OUT0: pin names not known; wires that end beside it: registrador_8bits_1_s
  Hex_Digit_Display hex_digit_display_3 (.value(in_9[3:0]));  // open: dp

  // Notes on the sheet:
  //   Memória de 64 endereços que guardam 8 bits cada
  //   Memória de 16 endereços que guardam 8 bits cada
  //   Registrador de 8 bits
  //   por trás de cada endereço existe um registrador
  //   << Memória sendo acessada
  //   << Memória sendo acessada
endmodule

module registrador_8bits (
  input  [7:0] A,
  input  clock,
  input  write,
  input  read,
  output [7:0] S
);

  wire controlled_buffer_1_out, controlled_buffer_10_out, d_ff_1_q, d_ff_2_q, d_ff_3_q, d_ff_4_q, d_ff_5_q,
       d_ff_6_q, d_ff_7_q, d_ff_8_q;

  assign controlled_buffer_1_out = write ? clock : 1'bz;  // Controlled_Buffer controlled_buffer_1
  D_Flip_Flop d_ff_1 (.D(A[0]), .clk(controlled_buffer_1_out), .Q(d_ff_1_q));  // open: Qn, preset, reset
  D_Flip_Flop d_ff_2 (.D(A[1]), .clk(controlled_buffer_1_out), .Q(d_ff_2_q));  // open: Qn, preset, reset
  D_Flip_Flop d_ff_3 (.D(A[2]), .clk(controlled_buffer_1_out), .Q(d_ff_3_q));  // open: Qn, preset, reset
  D_Flip_Flop d_ff_4 (.D(A[3]), .clk(controlled_buffer_1_out), .Q(d_ff_4_q));  // open: Qn, preset, reset
  D_Flip_Flop d_ff_5 (.D(A[4]), .clk(controlled_buffer_1_out), .Q(d_ff_5_q));  // open: Qn, preset, reset
  D_Flip_Flop d_ff_6 (.D(A[5]), .clk(controlled_buffer_1_out), .Q(d_ff_6_q));  // open: Qn, preset, reset
  D_Flip_Flop d_ff_7 (.D(A[6]), .clk(controlled_buffer_1_out), .Q(d_ff_7_q));  // open: Qn, preset, reset
  D_Flip_Flop d_ff_8 (.D(A[7]), .clk(controlled_buffer_1_out), .Q(d_ff_8_q));  // open: Qn, preset, reset
  assign S[0] = controlled_buffer_10_out ? d_ff_1_q : 1'bz;  // Controlled_Buffer controlled_buffer_2
  assign S[1] = controlled_buffer_10_out ? d_ff_2_q : 1'bz;  // Controlled_Buffer controlled_buffer_3
  assign S[2] = controlled_buffer_10_out ? d_ff_3_q : 1'bz;  // Controlled_Buffer controlled_buffer_4
  assign S[3] = controlled_buffer_10_out ? d_ff_4_q : 1'bz;  // Controlled_Buffer controlled_buffer_5
  assign S[4] = controlled_buffer_10_out ? d_ff_5_q : 1'bz;  // Controlled_Buffer controlled_buffer_6
  assign S[5] = controlled_buffer_10_out ? d_ff_6_q : 1'bz;  // Controlled_Buffer controlled_buffer_7
  assign S[6] = controlled_buffer_10_out ? d_ff_7_q : 1'bz;  // Controlled_Buffer controlled_buffer_8
  assign S[7] = controlled_buffer_10_out ? d_ff_8_q : 1'bz;  // Controlled_Buffer controlled_buffer_9
  assign controlled_buffer_10_out = read ? clock : 1'bz;  // Controlled_Buffer controlled_buffer_10
endmodule

module memoria_16x8 (
  input  clock,
  input  [7:0] IN1,
  input  read,
  input  write,
  input  [3:0] adress,
  output [7:0] S
);

  wire [1:0] demultiplexer_1_out0, demultiplexer_1_out1, demultiplexer_1_out2, demultiplexer_1_out3,
       demultiplexer_1_out4, demultiplexer_1_out5, demultiplexer_1_out6, demultiplexer_1_out7,
       demultiplexer_1_out8, demultiplexer_1_out9, demultiplexer_1_out10, demultiplexer_1_out11,
       demultiplexer_1_out12, demultiplexer_1_out13, demultiplexer_1_out14, demultiplexer_1_out15;
  wire [7:0] R0_s, R1_s, R2_s, R3_s, R4_s, R5_s, R6_s, R7_s, R8_s, R9_s, R10_s, R11_s, R12_s, R13_s, R14_s,
       R15_s;

  Demultiplexer #(.select(4), .width(2)) demultiplexer_1 (
    .out0(demultiplexer_1_out0), .out1(demultiplexer_1_out1), .out2(demultiplexer_1_out2),
    .out3(demultiplexer_1_out3), .out4(demultiplexer_1_out4), .out5(demultiplexer_1_out5),
    .out6(demultiplexer_1_out6), .out7(demultiplexer_1_out7), .out8(demultiplexer_1_out8),
    .out9(demultiplexer_1_out9), .out10(demultiplexer_1_out10), .out11(demultiplexer_1_out11),
    .out12(demultiplexer_1_out12), .out13(demultiplexer_1_out13), .out14(demultiplexer_1_out14),
    .out15(demultiplexer_1_out15), .in({write, read}), .sel(adress));
  registrador_8bits R0 (
    .clock(clock), .write(demultiplexer_1_out0[1]), .A(IN1), .read(demultiplexer_1_out0[0]), .S(R0_s));
  registrador_8bits R1 (
    .clock(clock), .write(demultiplexer_1_out1[1]), .A(IN1), .read(demultiplexer_1_out1[0]), .S(R1_s));
  registrador_8bits R2 (
    .clock(clock), .write(demultiplexer_1_out2[1]), .A(IN1), .read(demultiplexer_1_out2[0]), .S(R2_s));
  registrador_8bits R3 (
    .clock(clock), .write(demultiplexer_1_out3[1]), .A(IN1), .read(demultiplexer_1_out3[0]), .S(R3_s));
  registrador_8bits R4 (
    .clock(clock), .write(demultiplexer_1_out4[1]), .A(IN1), .read(demultiplexer_1_out4[0]), .S(R4_s));
  registrador_8bits R5 (
    .clock(clock), .write(demultiplexer_1_out5[1]), .A(IN1), .read(demultiplexer_1_out5[0]), .S(R5_s));
  registrador_8bits R6 (
    .clock(clock), .write(demultiplexer_1_out6[1]), .A(IN1), .read(demultiplexer_1_out6[0]), .S(R6_s));
  registrador_8bits R7 (
    .clock(clock), .write(demultiplexer_1_out7[1]), .A(IN1), .read(demultiplexer_1_out7[0]), .S(R7_s));
  registrador_8bits R8 (
    .clock(clock), .write(demultiplexer_1_out8[1]), .A(IN1), .read(demultiplexer_1_out8[0]), .S(R8_s));
  registrador_8bits R9 (
    .clock(clock), .write(demultiplexer_1_out9[1]), .A(IN1), .read(demultiplexer_1_out9[0]), .S(R9_s));
  registrador_8bits R10 (
    .clock(clock), .write(demultiplexer_1_out10[1]), .A(IN1), .read(demultiplexer_1_out10[0]), .S(R10_s));
  registrador_8bits R11 (
    .clock(clock), .write(demultiplexer_1_out11[1]), .A(IN1), .read(demultiplexer_1_out11[0]), .S(R11_s));
  registrador_8bits R12 (
    .clock(clock), .write(demultiplexer_1_out12[1]), .A(IN1), .read(demultiplexer_1_out12[0]), .S(R12_s));
  registrador_8bits R13 (
    .clock(clock), .write(demultiplexer_1_out13[1]), .A(IN1), .read(demultiplexer_1_out13[0]), .S(R13_s));
  registrador_8bits R14 (
    .clock(clock), .write(demultiplexer_1_out14[1]), .A(IN1), .read(demultiplexer_1_out14[0]), .S(R14_s));
  registrador_8bits R15 (
    .clock(clock), .write(demultiplexer_1_out15[1]), .A(IN1), .read(demultiplexer_1_out15[0]), .S(R15_s));
  Multiplexer #(.select(4), .width(8)) multiplexer_1 (
    .in0(R0_s), .in1(R1_s), .in2(R2_s), .in3(R3_s), .in4(R4_s), .in5(R5_s), .in6(R6_s), .in7(R7_s),
    .in8(R8_s), .in9(R9_s), .in10(R10_s), .in11(R11_s), .in12(R12_s), .in13(R13_s), .in14(R14_s),
    .in15(R15_s), .out(S), .sel(adress));
endmodule

module memoria_64x8 (
  input  clk,
  input  [7:0] IN1,
  input  write,
  input  read,
  input  [5:0] Adress,
  output [7:0] OUT1
);

  wire demultiplexer_1_out0, demultiplexer_1_out1, demultiplexer_1_out2, demultiplexer_1_out3;
  wire [1:0] controlled_buffer_1_out, controlled_buffer_2_out, controlled_buffer_3_out,
       controlled_buffer_4_out;
  wire [7:0] R0_16x8_s, R1_16x8_s, R2_16x8_s, R3_16x8_s;

  Demultiplexer #(.select(2)) demultiplexer_1 (
    .out0(demultiplexer_1_out0), .out1(demultiplexer_1_out1), .out2(demultiplexer_1_out2),
    .out3(demultiplexer_1_out3), .in(1'b1), .sel(Adress[5:4]));
  assign controlled_buffer_1_out = demultiplexer_1_out0 ? {read, write} : 2'bz;  // Controlled_Buffer controlled_buffer_1
  assign controlled_buffer_2_out = demultiplexer_1_out1 ? {read, write} : 2'bz;  // Controlled_Buffer controlled_buffer_2
  assign controlled_buffer_3_out = demultiplexer_1_out2 ? {read, write} : 2'bz;  // Controlled_Buffer controlled_buffer_3
  assign controlled_buffer_4_out = demultiplexer_1_out3 ? {read, write} : 2'bz;  // Controlled_Buffer controlled_buffer_4
  memoria_16x8 R0_16x8 (
    .read(controlled_buffer_1_out[1]), .write(controlled_buffer_1_out[0]), .adress(Adress[3:0]), .IN1(IN1),
    .clock(clk), .S(R0_16x8_s));
  memoria_16x8 R1_16x8 (
    .read(controlled_buffer_2_out[1]), .write(controlled_buffer_2_out[0]), .adress(Adress[3:0]), .IN1(IN1),
    .clock(clk), .S(R1_16x8_s));
  memoria_16x8 R2_16x8 (
    .read(controlled_buffer_3_out[1]), .write(controlled_buffer_3_out[0]), .adress(Adress[3:0]), .IN1(IN1),
    .clock(clk), .S(R2_16x8_s));
  memoria_16x8 R3_16x8 (
    .read(controlled_buffer_4_out[1]), .write(controlled_buffer_4_out[0]), .adress(Adress[3:0]), .IN1(IN1),
    .clock(clk), .S(R3_16x8_s));
  Multiplexer #(.select(2), .width(8)) multiplexer_1 (
    .in0(R0_16x8_s), .in1(R1_16x8_s), .in2(R2_16x8_s), .in3(R3_16x8_s), .out(OUT1), .sel(Adress[5:4]));
endmodule
